// Logisim project operations on a RAM chip.circ as structural Verilog: 5 circuits, main circuit operations 4-2 bit RAM
module encode_op_main (
  input  A0,
  input  A1,
  input  Start,
  input  EN,
  input  B0,
  input  B1,
  input  C0,
  input  C1,
  input  D0,
  input  D1,
  input  _1st,
  input  _2nd,
  input  in_13,
  input  in_14,
  input  in_15,
  input  in_16,
  input  in_17,
  input  in_18,
  input  in_19,
  input  in_20
);

  wire n2_4_bit_ram_chips_to_try_it_out_1_n0_2, n2_4_bit_ram_chips_to_try_it_out_1_n1_2,
       n2_4_bit_ram_chips_to_try_it_out_1_n2_2, n2_4_bit_ram_chips_to_try_it_out_1_n3_2,
       n2_4_bit_ram_chips_to_try_it_out_1_s0_2, n2_4_bit_ram_chips_to_try_it_out_1_s1_2,
       n2_4_bit_ram_chips_to_try_it_out_1_s2_2, n2_4_bit_ram_chips_to_try_it_out_1_s3_2,
       n2_4_bit_ram_chips_to_try_it_out_1_x_y, n2_4_bit_ram_chips_to_try_it_out_1_x_y_2,
       n2_4_bit_ram_chips_to_try_it_out_1_x_y_3, operation_chart_1_comp, operation_chart_1_cpy,
       operation_chart_1_en_in, operation_chart_1_strt, operations_4_2bit_ram_encoding_1__1st_digit_out,
       operations_4_2bit_ram_encoding_1__2nd_digit_out;

  operations_4_2bit_RAM_encoding operations_4_2bit_ram_encoding_1 (
    .A0in(A0), .A1in(A1), .B0in(B0), .B1in(B1), .C0in(C0), .C1in(C1), .D0in(D0), .D1in(D1),
    .start_reset(Start), .EN(EN), ._1st(_1st), ._2nd(_2nd),
    ._1st_digit_out(operations_4_2bit_ram_encoding_1__1st_digit_out),
    ._2nd_digit_out(operations_4_2bit_ram_encoding_1__2nd_digit_out));
  operation_chart operation_chart_1 (
    ._1st_bit(operations_4_2bit_ram_encoding_1__1st_digit_out),
    ._2nd_bit(operations_4_2bit_ram_encoding_1__2nd_digit_out), .strt(operation_chart_1_strt),
    .comp(operation_chart_1_comp), .cpy(operation_chart_1_cpy), .EN_in(operation_chart_1_en_in));
  _2_4_bit_RAM_chips_to_try_it_out u_2_4_bit_ram_chips_to_try_it_out_1 (
    .EN_in(operation_chart_1_en_in), .S0(in_13), .S1(in_14), .S2(in_15), .S3(in_16),
    .cpy(operation_chart_1_cpy), .N0(in_17), .N1(in_18), .N2(in_19), .N3(in_20),
    .start(operation_chart_1_strt), .X_Y(n2_4_bit_ram_chips_to_try_it_out_1_x_y),
    .X_Y_2(n2_4_bit_ram_chips_to_try_it_out_1_x_y_2), .X_Y_3(n2_4_bit_ram_chips_to_try_it_out_1_x_y_3),
    .S0_2(n2_4_bit_ram_chips_to_try_it_out_1_s0_2), .S1_2(n2_4_bit_ram_chips_to_try_it_out_1_s1_2),
    .S2_2(n2_4_bit_ram_chips_to_try_it_out_1_s2_2), .S3_2(n2_4_bit_ram_chips_to_try_it_out_1_s3_2),
    .N0_2(n2_4_bit_ram_chips_to_try_it_out_1_n0_2), .N1_2(n2_4_bit_ram_chips_to_try_it_out_1_n1_2),
    .N2_2(n2_4_bit_ram_chips_to_try_it_out_1_n2_2), .N3_2(n2_4_bit_ram_chips_to_try_it_out_1_n3_2));  // open: reset

  // Notes on the sheet:
  //   operations
  //   00. start device and resets all chips (done)
  //   10 compare RAM
  //   01 cpy commmand (done)
  //   10 put data in(done) from this chip
  //   strt
  //   en_in
  //   cpy
endmodule

module _2_4_bit_RAM_chips_to_try_it_out (
  input  EN_in,
  input  S0,
  input  S1,
  input  S2,
  input  S3,
  input  reset,
  input  cpy,
  input  N0,
  input  N1,
  input  N2,
  input  N3,
  input  start,
  output S0_2,
  output S1_2,
  output S2_2,
  output S3_2,
  output N0_2,
  output N1_2,
  output N2_2,
  output N3_2,
  output X_Y,
  output X_Y_2,
  output X_Y_3
);

  wire controlled_buffer_1_out, controlled_buffer_2_out, controlled_buffer_3_out, controlled_buffer_4_out,
       controlled_buffer_5_out, main_1_cpy_0, main_1_cpy_1, main_1_cpy_2, main_1_cpy_3, main_1_reset_signal,
       main_2_cpy_0, n2_pulsers_1__2_pulse, not_1_out, or_1_out, or_2_out, or_3_out, or_4_out, or_5_out,
       or_6_out, or_7_out;

  or or_1 (or_1_out, reset, not_1_out);
  or or_2 (or_2_out, cpy, controlled_buffer_1_out);
  not not_1 (not_1_out, controlled_buffer_1_out);
  assign controlled_buffer_1_out = start ? n2_pulsers_1__2_pulse : 1'bz;  // Controlled_Buffer controlled_buffer_1
  _2_pulsers u_2_pulsers_1 (.pulse_input(start), ._2_pulse(n2_pulsers_1__2_pulse));
  or or_3 (or_3_out, or_1_out, main_1_reset_signal);
  or or_4 (or_4_out, N0, main_1_cpy_3);
  or or_5 (or_5_out, N1, main_1_cpy_2);
  or or_6 (or_6_out, N2, main_1_cpy_1);
  or or_7 (or_7_out, N3, main_1_cpy_0);
  assign controlled_buffer_2_out = EN_in ? S0 : 1'bz;  // Controlled_Buffer controlled_buffer_2
  assign controlled_buffer_3_out = EN_in ? S1 : 1'bz;  // Controlled_Buffer controlled_buffer_3
  assign controlled_buffer_4_out = EN_in ? S2 : 1'bz;  // Controlled_Buffer controlled_buffer_4
  assign controlled_buffer_5_out = EN_in ? S3 : 1'bz;  // Controlled_Buffer controlled_buffer_5
  _4_bit_RAM_main main_1 (
    .reset(or_1_out), .cpy(or_2_out), .s0(controlled_buffer_2_out), .s1(controlled_buffer_3_out),
    .s2(controlled_buffer_4_out), .s3(controlled_buffer_5_out), .S0_out(S0_2), .S1_out(S1_2), .S2_out(S2_2),
    .S3_out(S3_2), .cpy_0(main_1_cpy_0), .cpy_1(main_1_cpy_1), .cpy_2(main_1_cpy_2), .cpy_3(main_1_cpy_3),
    .reset_signal(main_1_reset_signal));
  _4_bit_RAM_main main_2 (
    .reset(or_3_out), .s0(or_4_out), .s1(or_5_out), .s2(or_6_out), .s3(or_7_out), .S0_out(N0_2),
    .S1_out(N1_2), .S2_out(N2_2), .S3_out(N3_2), .cpy_0(main_2_cpy_0));  // open: cpy, cpy_1, cpy_2, cpy_3, reset_signal
  _4_bit_comparator u_4_bit_comparator_1 (
    .X0(S0_2), .X1(S1_2), .X2(S2_2), .X3(S3_2), .X_Y(X_Y), .X_Y_2(X_Y_2), .X_Y_3(X_Y_3), .Y0(N0_2),
    .Y1(N1_2), .Y2(N2_2), .Y3(N3_2));

  // Notes on the sheet:
  //   start button
  //   use decoder for operations:
  //   00. start device and resets all chips (done)
  //   10 compare RAM
  //   01 cpy commmand (done)
  //   10 put data in(done) from this chip
  //   8 bit RAM options and computer
  //   4 bit RAM
  //   4 bit RAM
  //   4 bit compare
endmodule

module operations_4_2_bit_RAM (
  input  EN,
  input  _1st_bit,
  input  _2nd_bit,
  input  D1in,
  input  D0in,
  input  C1in,
  input  C0in,
  input  B1in,
  input  B0in,
  input  A1in,
  input  A0in,
  input  start,
  output D1,
  output D0,
  output C1,
  output C0,
  output B1,
  output B0,
  output A1,
  output A0
);

  wire controlled_buffer_9_out, main_1_s0_out, main_1_s1_out, main_2_s0_out, main_2_s1_out, main_3_s0_out,
       main_3_s1_out, main_4_s0_out, main_4_s1_out, main_5_out_0, main_5_out_1, main_5_out_2, main_5_out_3,
       n2_pulsers_1__2_pulse, not_1_out;

  assign A1 = main_5_out_0 ? main_1_s1_out : 1'bz;  // Controlled_Buffer controlled_buffer_1
  assign A0 = main_5_out_0 ? main_1_s0_out : 1'bz;  // Controlled_Buffer controlled_buffer_2
  _2_bit_RAM_main main_1 (
    .reset(not_1_out), .cpy(controlled_buffer_9_out), .s0(D1in), .s1(D0in), .S0_out(main_1_s0_out),
    .S1_out(main_1_s1_out));  // open: cpy_0, cpy_1, reset_signal
  assign B0 = main_5_out_1 ? main_2_s0_out : 1'bz;  // Controlled_Buffer controlled_buffer_3
  _2_bit_RAM_main main_2 (
    .reset(not_1_out), .cpy(controlled_buffer_9_out), .s0(C1in), .s1(C0in), .S0_out(main_2_s0_out),
    .S1_out(main_2_s1_out));  // open: cpy_0, cpy_1, reset_signal
  assign B1 = main_5_out_1 ? main_2_s1_out : 1'bz;  // Controlled_Buffer controlled_buffer_4
  not not_1 (not_1_out, controlled_buffer_9_out);
  _2_bit_RAM_main main_3 (
    .reset(not_1_out), .cpy(controlled_buffer_9_out), .s0(B1in), .s1(B0in), .S0_out(main_3_s0_out),
    .S1_out(main_3_s1_out));  // open: cpy_0, cpy_1, reset_signal
  assign C1 = main_5_out_2 ? main_3_s1_out : 1'bz;  // Controlled_Buffer controlled_buffer_5
  assign C0 = main_5_out_2 ? main_3_s0_out : 1'bz;  // Controlled_Buffer controlled_buffer_6
  assign D1 = main_5_out_3 ? main_4_s1_out : 1'bz;  // Controlled_Buffer controlled_buffer_7
  assign D0 = main_5_out_3 ? main_4_s0_out : 1'bz;  // Controlled_Buffer controlled_buffer_8
  _2_bit_RAM_main main_4 (
    .reset(not_1_out), .cpy(controlled_buffer_9_out), .s0(A1in), .s1(A0in), .S0_out(main_4_s0_out),
    .S1_out(main_4_s1_out));  // open: cpy_0, cpy_1, reset_signal
  _2_4_DEC_main main_5 (
    .S1(_2nd_bit), .S0(_1st_bit), .E(EN), .out_0(main_5_out_0), .out_1(main_5_out_1), .out_2(main_5_out_2),
    .out_3(main_5_out_3));
  assign controlled_buffer_9_out = start ? n2_pulsers_1__2_pulse : 1'bz;  // Controlled_Buffer controlled_buffer_9
  _2_pulsers u_2_pulsers_1 (.pulse_input(start), ._2_pulse(n2_pulsers_1__2_pulse));

  // Notes on the sheet:
  //   1st 2nd
  //   00 A
  //   10 B
  //   01 C
  //   11 D
  //   each 2 bit RAM is used to create an operation
  //   All four together make it possible to do 4 operations in one go
  //   **more added in operations 4-2bit RAM encoding**
  //   start button
endmodule

module operation_chart (
  input  _1st_bit,
  input  _2nd_bit,
  output strt,
  output comp,
  output cpy,
  output EN_in
);

  wire not_1_out, not_2_out;

  not not_1 (not_1_out, _1st_bit);
  not not_2 (not_2_out, _2nd_bit);
  and and_1 (strt, not_1_out, not_2_out);
  and and_2 (comp, _1st_bit, not_2_out);
  and and_3 (cpy, not_1_out, _2nd_bit);
  and and_4 (EN_in, _1st_bit, _2nd_bit);

  // Notes on the sheet:
  //   00. start device and resets all chips (done)
  //   10 compare RAM
  //   01 cpy commmand (done)
  //   11 put data in(done) from this chip
endmodule

module operations_4_2bit_RAM_encoding (
  input  start_reset,
  input  EN,
  input  A0in,
  input  A1in,
  input  B0in,
  input  B1in,
  input  C0in,
  input  C1in,
  input  D0in,
  input  D1in,
  input  _1st,
  input  _2nd,
  output _1st_digit_out,
  output _2nd_digit_out
);

  wire operations_4_2_bit_ram_1_a0, operations_4_2_bit_ram_1_a1, operations_4_2_bit_ram_1_b0,
       operations_4_2_bit_ram_1_b1, operations_4_2_bit_ram_1_c0, operations_4_2_bit_ram_1_c1,
       operations_4_2_bit_ram_1_d0, operations_4_2_bit_ram_1_d1;

  operations_4_2_bit_RAM operations_4_2_bit_ram_1 (
    .D1(operations_4_2_bit_ram_1_d1), .D0(operations_4_2_bit_ram_1_d0), .C1(operations_4_2_bit_ram_1_c1),
    .C0(operations_4_2_bit_ram_1_c0), .B1(operations_4_2_bit_ram_1_b1), .B0(operations_4_2_bit_ram_1_b0),
    .A1(operations_4_2_bit_ram_1_a1), .A0(operations_4_2_bit_ram_1_a0), .start(start_reset), .EN(EN),
    ._1st_bit(_2nd), ._2nd_bit(_1st), .D1in(D1in), .D0in(D0in), .C1in(C1in), .C0in(C0in), .B1in(B1in),
    .B0in(B0in), .A1in(A1in), .A0in(A0in));
  or or_1 (_1st_digit_out, operations_4_2_bit_ram_1_d1, operations_4_2_bit_ram_1_a1, operations_4_2_bit_ram_1_b1, operations_4_2_bit_ram_1_c1);
  or or_2 (_2nd_digit_out, operations_4_2_bit_ram_1_a0, operations_4_2_bit_ram_1_b0, operations_4_2_bit_ram_1_c0, operations_4_2_bit_ram_1_d0);

  // Notes on the sheet:
  //   1st 2nd
  //   00 A
  //   10 B
  //   01 C
  //   11 D
  //   shows contents of 4-2bit RAM chips
endmodule
