// Logisim project 2 led.circ as structural Verilog: 1 circuit, main circuit main
module main (
);

  wire clock_1_out, not_1_out;

  Clock #(.highDuration(1), .lowDuration(1)) clock_1 (.out(clock_1_out));
  not not_1 (not_1_out, clock_1_out);
  LED led_1 (.in(clock_1_out));
  LED led_2 (.in(not_1_out));
endmodule
