// Logisim project 6bit_ALU.circ as structural Verilog: 1 circuit, main circuit main
module main (
  input  F1,
  input  F0,
  input  ENB,
  input  ENA,
  input  INVA,
  input  INC,
  input  [5:0] A,
  input  [5:0] B,
  output [5:0] OUTPUT,
  output OUTC
);

  wire alu_1_outc, alu_2_outc, alu_3_outc, alu_4_outc, alu_5_outc;

  // Probe on A
  // Probe on B
  ALU alu_1 (
    .INVA(INVA), .A(A[0]), .ENA(ENA), .B(B[0]), .ENB(ENB), .F0(F0), .F1(F1), .INC(INC), .OUTC(alu_1_outc),
    .OUTPUT(OUTPUT[0]));
  ALU alu_2 (
    .INVA(INVA), .A(A[1]), .ENA(ENA), .B(B[1]), .ENB(ENB), .F0(F0), .F1(F1), .INC(alu_1_outc),
    .OUTC(alu_2_outc), .OUTPUT(OUTPUT[1]));
  ALU alu_3 (
    .INVA(INVA), .A(A[2]), .ENA(ENA), .B(B[2]), .ENB(ENB), .F0(F0), .F1(F1), .INC(alu_2_outc),
    .OUTC(alu_3_outc), .OUTPUT(OUTPUT[2]));
  ALU alu_4 (
    .INVA(INVA), .A(A[3]), .ENA(ENA), .B(B[3]), .ENB(ENB), .F0(F0), .F1(F1), .INC(alu_3_outc),
    .OUTC(alu_4_outc), .OUTPUT(OUTPUT[3]));
  ALU alu_5 (
    .INVA(INVA), .A(A[4]), .ENA(ENA), .B(B[4]), .ENB(ENB), .F0(F0), .F1(F1), .INC(alu_4_outc),
    .OUTC(alu_5_outc), .OUTPUT(OUTPUT[4]));
  ALU alu_6 (
    .INVA(INVA), .A(A[5]), .ENA(ENA), .B(B[5]), .ENB(ENB), .F0(F0), .F1(F1), .INC(alu_5_outc), .OUTC(OUTC),
    .OUTPUT(OUTPUT[5]));
  // Probe on OUTPUT
endmodule
