// Logisim project ALU.circ as structural Verilog: 10 circuits, main circuit ALU
module _4_bit_logical_ALU (
  input  [5:0] F,
  input  ENA,
  input  ENB,
  input  [3:0] A,
  input  [3:0] B,
  output [3:0] out_6
);

  logical_ALU logical_alu_1 (.F(F), .ENA(ENA), .ENB(ENB), .A(A[0]), .B(B[0]), .out(out_6[0]));
  logical_ALU logical_alu_2 (.F(F), .ENA(ENA), .ENB(ENB), .A(A[1]), .B(B[1]), .out(out_6[1]));
  logical_ALU logical_alu_3 (.F(F), .ENA(ENA), .ENB(ENB), .A(A[2]), .B(B[2]), .out(out_6[2]));
  logical_ALU logical_alu_4 (.F(F), .ENA(ENA), .ENB(ENB), .A(A[3]), .B(B[3]), .out(out_6[3]));

  // Notes on the sheet:
  //   4 bit logical ALU
  //   7 different options create a decoder for logical ALU
endmodule

module ALU (
  input  INC,
  input  INVA,
  input  A,
  input  ENA,
  input  B,
  input  ENB,
  input  F0,
  input  F1,
  output OUTPUT,
  output OUTC
);

  wire and_1_out, and_2_out, and_3_out, and_4_out, and_5_out, and_6_out, and_7_out, and_8_out, and_9_out,
       and_10_out, and_11_out, and_12_out, and_13_out, not_1_out, not_2_out, not_3_out, not_4_out, not_5_out,
       or_1_out, xor_1_out, xor_2_out, xor_3_out;

  and and_1 (and_1_out, A, ENA);
  and and_2 (and_2_out, B, ENB);
  not not_1 (not_1_out, F0);
  not not_2 (not_2_out, F1);
  not not_3 (not_3_out, F0);
  not not_4 (not_4_out, F1);
  xor xor_1 (xor_1_out, INVA, and_1_out);
  and and_3 (and_3_out, not_1_out, not_2_out);
  and and_4 (and_4_out, not_3_out, F1);
  and and_5 (and_5_out, F0, not_4_out);
  and and_6 (and_6_out, F0, F1);
  and and_7 (and_7_out, xor_1_out, and_2_out);
  or or_1 (or_1_out, xor_1_out, and_2_out);
  not not_5 (not_5_out, and_2_out);
  and and_8 (and_8_out, and_6_out, and_2_out, xor_1_out);
  and and_9 (and_9_out, and_7_out, and_3_out);
  and and_10 (and_10_out, or_1_out, and_4_out);
  and and_11 (and_11_out, not_5_out, and_5_out);
  xor xor_2 (xor_2_out, and_2_out, xor_1_out);
  and and_12 (and_12_out, and_6_out, xor_2_out, INC, INC);
  or or_2 (OUTC, and_8_out, and_12_out);
  xor xor_3 (xor_3_out, INC, xor_2_out);
  and and_13 (and_13_out, xor_3_out, and_6_out);
  or or_3 (OUTPUT, and_9_out, and_10_out, and_11_out, and_13_out);

  // Notes on the sheet:
  //   AB
  //   A or B
  //   Not B
  //   A plus B
endmodule

module logical_ALU (
  input  [5:0] F,
  input  ENA,
  input  ENB,
  input  A,
  input  B,
  output out
);

  wire a_b_1_a_b, a_b_2_a_b, a_nand_b_1_a_b, a_nor_b_1_a_b, a_xnor_b_1_a_xnor_b, a_xor_b_1_a_b;

  A_B a_b_1 (.EN(F[0]), .ENA(ENA), .ENB(ENB), .A(A), .B(B), .A_B(a_b_1_a_b));
  A_B_2 a_b_2 (.EN(F[1]), .ENA(ENA), .ENB(ENB), .A(A), .B(B), .A_B(a_b_2_a_b));
  A_NAND_B a_nand_b_1 (.EN(F[2]), .ENA(ENA), .ENB(ENB), .A(A), .B(B), .A_B(a_nand_b_1_a_b));
  A_NOR_B a_nor_b_1 (.EN(F[3]), .ENA(ENA), .ENB(ENB), .A(A), .B(B), .A_B(a_nor_b_1_a_b));
  A_XOR_B a_xor_b_1 (.EN(F[4]), .ENA(ENA), .ENB(ENB), .A(A), .B(B), .A_B(a_xor_b_1_a_b));
  A_XNOR_B a_xnor_b_1 (.EN(F[5]), .ENA(ENA), .ENB(ENB), .A(A), .B(B), .A_xnor_B(a_xnor_b_1_a_xnor_b));
  or or_1 (out, a_b_1_a_b, a_b_2_a_b, a_nand_b_1_a_b, a_nor_b_1_a_b, a_xor_b_1_a_b, a_xnor_b_1_a_xnor_b);

  // Notes on the sheet:
  //   Logical ALU
  //   use nor gate for not A or not B
  //   A nor B is same as ~A and ~B
endmodule

module A_B (
  input  EN,
  input  ENA,
  input  ENB,
  input  A,
  input  B,
  output A_B
);

  wire and_1_out, and_2_out, controlled_buffer_1_out, controlled_buffer_2_out;

  and and_1 (and_1_out, EN, ENA);
  and and_2 (and_2_out, EN, ENB);
  assign controlled_buffer_1_out = and_1_out ? A : 1'bz;  // Controlled_Buffer controlled_buffer_1
  assign controlled_buffer_2_out = and_2_out ? B : 1'bz;  // Controlled_Buffer controlled_buffer_2
  and and_3 (A_B, controlled_buffer_1_out, controlled_buffer_2_out);

  // Notes on the sheet:
  //   A and B 
endmodule

module A_B_2 (
  input  EN,
  input  ENA,
  input  ENB,
  input  A,
  input  B,
  output A_B
);

  wire and_1_out, and_2_out, controlled_buffer_1_out, controlled_buffer_2_out;

  and and_1 (and_1_out, EN, ENA);
  and and_2 (and_2_out, EN, ENB);
  assign controlled_buffer_1_out = and_1_out ? A : 1'bz;  // Controlled_Buffer controlled_buffer_1
  assign controlled_buffer_2_out = and_2_out ? B : 1'bz;  // Controlled_Buffer controlled_buffer_2
  or or_1 (A_B, controlled_buffer_1_out, controlled_buffer_2_out);
endmodule

module A_NAND_B (
  input  EN,
  input  ENA,
  input  ENB,
  input  A,
  input  B,
  output A_B
);

  wire and_1_out, and_2_out, controlled_buffer_1_out, controlled_buffer_2_out;

  and and_1 (and_1_out, EN, ENA);
  and and_2 (and_2_out, EN, ENB);
  assign controlled_buffer_1_out = and_1_out ? A : 1'bz;  // Controlled_Buffer controlled_buffer_1
  assign controlled_buffer_2_out = and_2_out ? B : 1'bz;  // Controlled_Buffer controlled_buffer_2
  nand nand_1 (A_B, controlled_buffer_1_out, controlled_buffer_2_out);
endmodule

module A_NOR_B (
  input  EN,
  input  ENA,
  input  ENB,
  input  A,
  input  B,
  output A_B
);

  wire and_1_out, and_2_out, controlled_buffer_1_out, controlled_buffer_2_out;

  and and_1 (and_1_out, EN, ENA);
  and and_2 (and_2_out, EN, ENB);
  assign controlled_buffer_1_out = and_1_out ? A : 1'bz;  // Controlled_Buffer controlled_buffer_1
  assign controlled_buffer_2_out = and_2_out ? B : 1'bz;  // Controlled_Buffer controlled_buffer_2
  nor nor_1 (A_B, controlled_buffer_1_out, controlled_buffer_2_out);
endmodule

module A_XOR_B (
  input  EN,
  input  ENA,
  input  ENB,
  input  A,
  input  B,
  output A_B
);

  wire and_1_out, and_2_out, controlled_buffer_1_out, controlled_buffer_2_out;

  and and_1 (and_1_out, EN, ENA);
  and and_2 (and_2_out, EN, ENB);
  assign controlled_buffer_1_out = and_1_out ? A : 1'bz;  // Controlled_Buffer controlled_buffer_1
  assign controlled_buffer_2_out = and_2_out ? B : 1'bz;  // Controlled_Buffer controlled_buffer_2
  xor xor_1 (A_B, controlled_buffer_1_out, controlled_buffer_2_out);
endmodule

module A_XNOR_B (
  input  EN,
  input  ENA,
  input  ENB,
  input  A,
  input  B,
  output A_xnor_B
);

  wire and_1_out, and_2_out, controlled_buffer_1_out, controlled_buffer_2_out;

  and and_1 (and_1_out, EN, ENA);
  and and_2 (and_2_out, EN, ENB);
  assign controlled_buffer_1_out = and_1_out ? A : 1'bz;  // Controlled_Buffer controlled_buffer_1
  assign controlled_buffer_2_out = and_2_out ? B : 1'bz;  // Controlled_Buffer controlled_buffer_2
  xnor xnor_1 (A_xnor_B, controlled_buffer_1_out, controlled_buffer_2_out);
endmodule

module calculations (
  input  [1:0] in_1,
  input  in_2,
  input  in_3,
  input  in_4,
  output out_5
);

  wire clock_1_out;

  Clock #(.highDuration(1), .lowDuration(1)) clock_1 (.out(clock_1_out));
  RAM #(.addrWidth(2), .dataWidth(1), .bus("combined")) ram_1 (
    .addr(in_1), .data(out_5), .sel(in_2), .clk(clock_1_out), .ld(in_3), .clr(in_4));
endmodule
