// Logisim project 1-bit COM.circ as structural Verilog: 1 circuit, main circuit main
module main (
  input  X_i,
  input  Y_i,
  output X_Y,
  output X_Y_2,
  output X_Y_3
);

  wire not_1_out, not_2_out;

  not not_1 (not_1_out, X_i);
  not not_2 (not_2_out, Y_i);
  and and_1 (X_Y, X_i, not_2_out);
  and and_2 (X_Y_3, not_1_out, Y_i);
  xnor xnor_1 (X_Y_2, X_i, Y_i);

  // Notes on the sheet:
  //   1 bit comparitor 
  //   Michael Chrisco
endmodule
