// Logisim project 2-1 MUX.circ as structural Verilog: 1 circuit, main circuit main
module main (
  input  In_0,
  input  IN_1,
  input  E,
  input  S0,
  output Out
);

  wire and_1_out, and_2_out, not_1_out, or_1_out;

  not not_1 (not_1_out, S0);
  and and_1 (and_1_out, In_0, not_1_out);
  and and_2 (and_2_out, IN_1, S0);
  assign Out = E ? or_1_out : 1'bz;  // Controlled_Buffer controlled_buffer_1
  or or_1 (or_1_out, and_1_out, and_2_out);
endmodule
