// Logisim project 2-4 DEC.circ as structural Verilog: 1 circuit, main circuit main
module main (
  input  S1,
  input  S0,
  input  E,
  output out_0,
  output out_1,
  output out_2,
  output out_3
);

  wire and_1_out, and_2_out, and_3_out, and_4_out, not_1_out, not_2_out;

  not not_1 (not_1_out, S1);
  not not_2 (not_2_out, S0);
  and and_1 (and_1_out, not_1_out, not_2_out);
  and and_2 (and_2_out, not_1_out, S0);
  and and_3 (and_3_out, S1, not_2_out);
  and and_4 (and_4_out, S1, S0);
  assign out_0 = E ? and_1_out : 1'bz;  // Controlled_Buffer controlled_buffer_1
  assign out_1 = E ? and_2_out : 1'bz;  // Controlled_Buffer controlled_buffer_2
  assign out_2 = E ? and_3_out : 1'bz;  // Controlled_Buffer controlled_buffer_3
  assign out_3 = E ? and_4_out : 1'bz;  // Controlled_Buffer controlled_buffer_4
endmodule
