// Logisim project 4-1 MUX (1enable).circ as structural Verilog: 1 circuit, main circuit main
module main (
  input  In_0,
  input  In_1,
  input  In_2,
  input  In_3,
  input  E,
  input  S1,
  input  S2,
  output Out_0
);

  wire and_1_out, and_2_out, and_3_out, and_4_out, not_1_out, not_2_out, or_1_out;

  not not_1 (not_1_out, S2);
  not not_2 (not_2_out, S1);
  and and_1 (and_1_out, In_0, not_2_out, not_1_out);
  and and_2 (and_2_out, In_1, not_2_out, S2);
  and and_3 (and_3_out, In_2, S1, not_1_out);
  and and_4 (and_4_out, In_3, S1, S2);
  or or_1 (or_1_out, and_1_out, and_2_out, and_3_out, and_4_out);
  assign Out_0 = E ? or_1_out : 1'bz;  // Controlled_Buffer controlled_buffer_1

  // Notes on the sheet:
  //   4-1 MUX
  //   Michael Chrisco
endmodule
