// Logisim project 4-2 ENC.circ as structural Verilog: 2 circuits, main circuit 4-2 encoder
module _4_2_encoder (
  input  In_0,
  input  In_1,
  input  In_2,
  input  In_3,
  input  E,
  output V,
  output S0,
  output S1
);

  wire or_1_out, or_2_out, or_3_out;

  or or_1 (or_1_out, In_0, In_1, In_2, In_3);
  or or_2 (or_2_out, In_1, In_3);
  or or_3 (or_3_out, In_2, In_3);
  assign V = E ? or_1_out : 1'bz;  // Controlled_Buffer controlled_buffer_1
  assign S0 = E ? or_2_out : 1'bz;  // Controlled_Buffer controlled_buffer_2
  assign S1 = E ? or_3_out : 1'bz;  // Controlled_Buffer controlled_buffer_3

  // Notes on the sheet:
  //   4-to-2 encoder
  //   Michael Chrisco
endmodule

module w_o_enable (
  input  In_0,
  input  In_1,
  input  In_2,
  input  In_3,
  output V,
  output S0,
  output S1
);

  or or_1 (V, In_0, In_1, In_2, In_3);
  or or_2 (S0, In_1, In_3);
  or or_3 (S1, In_2, In_3);

  // Notes on the sheet:
  //   4-to-2 encoder without enable
  //   Michael Chrisco
endmodule
