// Logisim project 2bit_gray.circ as structural Verilog
module main (
  input  in_1,
  input  in_2,
  input  in_3,
  output out_4,
  output out_5
);
endmodule

module _00_01 (
  input  in_1,
  input  in_2,
  input  in_3,
  output out_4,
  output out_5
);
endmodule

module gray_2bit (
  input  a,
  input  b,
  input  c,
  output x,
  output y
);

  wire and_1_out, and_2_out, and_3_out, and_4_out, not_1_out, not_2_out, not_3_out;

  and and_1 (and_1_out, b, c);
  and and_2 (and_2_out, a, not_1_out);
  not not_1 (not_1_out, c);
  not not_2 (not_2_out, a);
  and and_3 (and_3_out, not_2_out, c);
  and and_4 (and_4_out, b, not_3_out);
  not not_3 (not_3_out, c);
  or or_1 (x, and_1_out, and_2_out);
  or or_2 (y, and_3_out, and_4_out);
endmodule
