// Logisim project up_down_binary counter.circ as structural Verilog
module main (
  input  _0_up_1_down,
  input  clock,
  input  in_3,
  output out_4,
  output out_5,
  output S0,
  output S1,
  output S2
);

  wire and_1_out, and_2_out, and_3_out, and_4_out, buffer_1_out, buffer_2_out, buffer_3_out,
       controlled_buffer_1_out, controlled_buffer_2_out, j_k_ff_1_qn, j_k_ff_2_qn, j_k_ff_3_qn, not_1_out,
       not_2_out, not_3_out, or_1_out, or_2_out;

  not not_1 (not_1_out, _0_up_1_down);
  J_K_Flip_Flop #(.trigger("rising")) j_k_ff_1 (
    .J(1'b1), .clk(clock), .K(1'b1), .Q(S0), .Qn(j_k_ff_1_qn), .reset(buffer_1_out));  // open: preset, en
  buf buffer_1 (buffer_1_out, buffer_2_out);
  buf buffer_2 (buffer_2_out, in_3);
  and and_1 (and_1_out, _0_up_1_down, S0);
  or or_1 (or_1_out, and_1_out, and_2_out);
  and and_2 (and_2_out, j_k_ff_1_qn, not_1_out);
  assign controlled_buffer_1_out = not_2_out ? or_1_out : 1'bz;  // Controlled_Buffer controlled_buffer_1
  not not_2 (not_2_out, in_3);
  and and_3 (and_3_out, _0_up_1_down, S1);
  J_K_Flip_Flop #(.trigger("rising")) j_k_ff_2 (
    .J(1'b1), .clk(controlled_buffer_1_out), .K(1'b1), .Q(S1), .Qn(j_k_ff_2_qn), .reset(buffer_3_out));  // open: preset, en
  and and_4 (and_4_out, j_k_ff_2_qn, not_1_out);
  buf buffer_3 (buffer_3_out, in_3);
  or or_2 (or_2_out, and_3_out, and_4_out);
  not not_3 (not_3_out, in_3);
  J_K_Flip_Flop #(.trigger("rising")) j_k_ff_3 (
    .J(1'b1), .clk(controlled_buffer_2_out), .K(1'b1), .Q(S2), .Qn(j_k_ff_3_qn), .reset(in_3));  // open: preset, en
  assign controlled_buffer_2_out = not_3_out ? or_2_out : 1'bz;  // Controlled_Buffer controlled_buffer_2
  and and_5 (out_4, _0_up_1_down, S2);
  and and_6 (out_5, j_k_ff_3_qn, not_1_out);

  // Notes on the sheet:
  //   Up/down binary counter
endmodule

module up_down_with_inputs (
  input  direction,
  output out_2,
  output out_3
);

  wire and_1_out, and_2_out, clock_out, n1_bit_ram_1_done, n1_bit_ram_2_done, not_1_out, not_2_out, or_1_out,
       undriven;

  not not_1 (not_1_out, direction);
  _1_bit_RAM u_1_bit_ram_1 (.set(undriven), .DONE(n1_bit_ram_1_done), .clock(clock_out), .out(out_2));
  not not_2 (not_2_out, out_2);
  Clock #(.highDuration(1), .lowDuration(1)) clock (.out(clock_out));
  and and_1 (and_1_out, direction, n1_bit_ram_1_done, out_2);
  and and_2 (and_2_out, not_2_out, n1_bit_ram_1_done, not_1_out);
  or or_1 (or_1_out, and_1_out, and_2_out);
  _1_bit_RAM u_1_bit_ram_2 (.set(or_1_out), .DONE(n1_bit_ram_2_done), .clock(clock_out), .out(out_3));

  // Notes on the sheet:
  //   not working
endmodule

module up_down_1_bit (
  input  direction,
  input  clock,
  output out
);

  wire and_1_out, and_2_out, j_k_ff_1_q, j_k_ff_1_qn, not_1_out;

  not not_1 (not_1_out, direction);
  J_K_Flip_Flop #(.trigger("rising")) j_k_ff_1 (
    .J(1'b1), .clk(clock), .K(1'b1), .Q(j_k_ff_1_q), .Qn(j_k_ff_1_qn));  // open: preset, en, reset
  and and_1 (and_1_out, direction, j_k_ff_1_q);
  and and_2 (and_2_out, j_k_ff_1_qn, not_1_out);
  or or_1 (out, and_1_out, and_2_out);

  // Notes on the sheet:
  //   not working
endmodule
