// Logisim project 0-9 counter.circ as structural Verilog: 2 circuits, main circuit combin
module combin (
  output S0,
  output S1,
  output S2,
  output S3,
  output out_5
);

  wire and_1_out, clock_1_out, j_k_ff_1_qn, j_k_ff_2_qn, j_k_ff_3_qn, j_k_ff_4_qn;

  Clock #(.highDuration(1), .lowDuration(1)) clock_1 (.out(clock_1_out));
  not not_1 (S0, j_k_ff_1_qn);
  J_K_Flip_Flop #(.trigger("rising")) j_k_ff_1 (
    .J(1'b1), .clk(clock_1_out), .K(1'b1), .Qn(j_k_ff_1_qn), .preset(and_1_out));  // open: Q, en, reset
  not not_2 (S1, j_k_ff_2_qn);
  J_K_Flip_Flop #(.trigger("rising")) j_k_ff_2 (
    .J(1'b1), .clk(j_k_ff_1_qn), .K(1'b1), .Qn(j_k_ff_2_qn), .preset(and_1_out));  // open: Q, en, reset
  not not_3 (S2, j_k_ff_3_qn);
  J_K_Flip_Flop #(.trigger("rising")) j_k_ff_3 (
    .J(1'b1), .clk(j_k_ff_2_qn), .K(1'b1), .Qn(j_k_ff_3_qn), .preset(and_1_out));  // open: Q, en, reset
  not not_4 (S3, j_k_ff_4_qn);
  J_K_Flip_Flop #(.trigger("rising")) j_k_ff_4 (
    .J(1'b1), .clk(j_k_ff_3_qn), .K(1'b1), .Qn(j_k_ff_4_qn), .preset(and_1_out));  // open: Q, en, reset
  and and_1 (and_1_out, S3, j_k_ff_3_qn, j_k_ff_2_qn, S0);
  and and_2 (out_5, S3, S1, S2, S0);

  // Notes on the sheet:
  //   a 0 to 9 counter with reset at 1001
  //   Michael Chrisco
endmodule

module _0_to_5 (
  input  in_1,
  output S0,
  output S1,
  output S2,
  output S3
);

  wire and_1_out, j_k_ff_1_qn, j_k_ff_2_qn, j_k_ff_3_qn, j_k_ff_4_qn;

  not not_1 (S0, j_k_ff_1_qn);
  J_K_Flip_Flop #(.trigger("rising")) j_k_ff_1 (
    .J(1'b1), .clk(in_1), .K(1'b1), .Qn(j_k_ff_1_qn), .preset(and_1_out));  // open: Q, en, reset
  not not_2 (S1, j_k_ff_2_qn);
  J_K_Flip_Flop #(.trigger("rising")) j_k_ff_2 (
    .J(1'b1), .clk(j_k_ff_1_qn), .K(1'b1), .Qn(j_k_ff_2_qn), .preset(and_1_out));  // open: Q, en, reset
  not not_3 (S2, j_k_ff_3_qn);
  J_K_Flip_Flop #(.trigger("rising")) j_k_ff_3 (
    .J(1'b1), .clk(j_k_ff_2_qn), .K(1'b1), .Qn(j_k_ff_3_qn), .preset(and_1_out));  // open: Q, en, reset
  not not_4 (S3, j_k_ff_4_qn);
  J_K_Flip_Flop #(.trigger("rising")) j_k_ff_4 (
    .J(1'b1), .clk(j_k_ff_3_qn), .K(1'b1), .Qn(j_k_ff_4_qn), .preset(and_1_out));  // open: Q, en, reset
  and and_1 (and_1_out, j_k_ff_4_qn, S2, S1, j_k_ff_1_qn);

  // Notes on the sheet:
  //   0 to 5 counter
  //   Michael Chrisco
endmodule
