// Logisim project LED final.circ as structural Verilog: 1 circuit, main circuit main
module main (
);

  _7_Segment_Display u_7_segment_display_1 ();  // open: g, f, a, b, e, d, c, dp
  _7_Segment_Display u_7_segment_display_2 ();  // open: g, f, a, b, e, d, c, dp
  _7_Segment_Display u_7_segment_display_3 ();  // open: g, f, a, b, e, d, c, dp
  _7_Segment_Display u_7_segment_display_4 ();  // open: g, f, a, b, e, d, c, dp

  // Notes on the sheet:
  //   0-9
  //   0-6
  //   1-9,0-2
  //   0-1 (combined in last circuit)
endmodule
