// Logisim project LED.circ as structural Verilog: 24 circuits, main circuit in 0
module main_clock (
  input  reset_current,
  input  manual_add_10_s
);

  wire all_in_1_out_0, all_in_1_out_1, all_in_1_out_2, all_in_1_out_3, all_in_1_out_4, all_in_1_out_5,
       all_in_1_out_6, all_in_2_out_0, all_in_2_out_1, all_in_2_out_2, all_in_2_out_3, all_in_2_out_4,
       all_in_2_out_5, all_in_2_out_6, all_in_3_out_0, all_in_3_out_1, all_in_3_out_2, all_in_3_out_3,
       all_in_3_out_4, all_in_3_out_5, all_in_3_out_6, all_in_4_out_0, all_in_4_out_1, all_in_4_out_2,
       all_in_4_out_3, all_in_4_out_4, all_in_4_out_5, all_in_4_out_6, clock_1_out, controlled_buffer_1_out,
       controlled_buffer_2_out, controlled_buffer_3_out, controlled_buffer_4_out, n0_5_counter_1_out_3,
       n0_5_counter_1_out_4, n0_5_counter_1_out_5, n0_5_counter_1_out_6, n0_5_counter_1_out_10,
       n0_9_counter_1_out_10, n0_9_counter_1_s0, n0_9_counter_1_s1, n0_9_counter_1_s2, n0_9_counter_1_s3,
       nand_1_out, new_0_12_counter_1_last_place_digit, new_0_12_counter_1_s0, new_0_12_counter_1_s1,
       new_0_12_counter_1_s2, new_0_12_counter_1_s3, not_1_out, undriven, undriven_2, undriven_3;

  Clock #(.highDuration(1), .lowDuration(1)) clock_1 (.out(clock_1_out));
  not not_1 (not_1_out, manual_add_10_s);
  ALL_IN all_in_1 (
    .S0(n0_9_counter_1_s3), .S1(n0_9_counter_1_s2), .S2(n0_9_counter_1_s1), .S3(n0_9_counter_1_s0),
    .out_0(all_in_1_out_0), .out_1(all_in_1_out_1), .out_2(all_in_1_out_2), .out_3(all_in_1_out_3),
    .out_4(all_in_1_out_4), .out_5(all_in_1_out_5), .out_6(all_in_1_out_6));
  _0_9_counter u_0_9_counter_1 (
    .clock(clock_1_out), .in_2(reset_current), .out_10(n0_9_counter_1_out_10), .S0(n0_9_counter_1_s0),
    .S1(n0_9_counter_1_s1), .S2(n0_9_counter_1_s2), .S3(n0_9_counter_1_s3));
  _0_5_counter u_0_5_counter_1 (
    .reset(reset_current), .out_4(n0_5_counter_1_out_4), .out_5(n0_5_counter_1_out_5),
    .out_6(n0_5_counter_1_out_6), .out_3(n0_5_counter_1_out_3), .in_1(nand_1_out),
    .out_10(n0_5_counter_1_out_10));
  nand nand_1 (nand_1_out, n0_9_counter_1_out_10, not_1_out);
  ALL_IN all_in_2 (
    .S0(n0_5_counter_1_out_3), .S1(n0_5_counter_1_out_6), .S2(n0_5_counter_1_out_5),
    .S3(n0_5_counter_1_out_4), .out_0(all_in_2_out_0), .out_1(all_in_2_out_1), .out_2(all_in_2_out_2),
    .out_3(all_in_2_out_3), .out_4(all_in_2_out_4), .out_5(all_in_2_out_5), .out_6(all_in_2_out_6));
  new_0_12_counter new_0_12_counter_1 (
    .last_place_digit(new_0_12_counter_1_last_place_digit), .clock(n0_5_counter_1_out_10),
    .S0(new_0_12_counter_1_s0), .S1(new_0_12_counter_1_s1), .S2(new_0_12_counter_1_s2),
    .S3(new_0_12_counter_1_s3));
  _7_Segment_Display u_7_segment_display_1 (
    .g(all_in_1_out_3), .f(all_in_1_out_2), .a(all_in_1_out_1), .b(all_in_1_out_0), .e(all_in_1_out_4),
    .d(all_in_1_out_5), .c(all_in_1_out_6));  // open: dp
  ALL_IN all_in_3 (
    .S0(new_0_12_counter_1_s3), .S1(new_0_12_counter_1_s2), .S2(new_0_12_counter_1_s1),
    .S3(new_0_12_counter_1_s0), .out_0(all_in_3_out_0), .out_1(all_in_3_out_1), .out_2(all_in_3_out_2),
    .out_3(all_in_3_out_3), .out_4(all_in_3_out_4), .out_5(all_in_3_out_5), .out_6(all_in_3_out_6));
  assign controlled_buffer_1_out = new_0_12_counter_1_last_place_digit ? new_0_12_counter_1_last_place_digit : 1'bz;  // Controlled_Buffer controlled_buffer_1
  assign controlled_buffer_2_out = new_0_12_counter_1_last_place_digit ? 1'b0 : 1'bz;  // Controlled_Buffer controlled_buffer_2
  assign controlled_buffer_3_out = new_0_12_counter_1_last_place_digit ? 1'b0 : 1'bz;  // Controlled_Buffer controlled_buffer_3
  assign controlled_buffer_4_out = new_0_12_counter_1_last_place_digit ? 1'b0 : 1'bz;  // Controlled_Buffer controlled_buffer_4
  _7_Segment_Display u_7_segment_display_2 (
    .g(all_in_2_out_3), .f(all_in_2_out_2), .a(all_in_2_out_1), .b(all_in_2_out_0), .e(all_in_2_out_4),
    .d(all_in_2_out_5), .c(all_in_2_out_6), .dp(undriven));
  _7_Segment_Display u_7_segment_display_3 (
    .g(all_in_2_out_3), .f(all_in_2_out_2), .a(all_in_2_out_1), .b(all_in_2_out_0), .e(all_in_2_out_4),
    .d(all_in_2_out_5), .c(all_in_2_out_6), .dp(undriven));
  _7_Segment_Display u_7_segment_display_4 (
    .g(all_in_3_out_3), .f(all_in_3_out_2), .a(all_in_3_out_1), .b(all_in_3_out_0), .e(all_in_3_out_4),
    .d(all_in_3_out_5), .c(all_in_3_out_6), .dp(undriven_2));
  ALL_IN all_in_4 (
    .S0(controlled_buffer_2_out), .S1(controlled_buffer_3_out), .S2(controlled_buffer_4_out),
    .S3(controlled_buffer_1_out), .out_0(all_in_4_out_0), .out_1(all_in_4_out_1), .out_2(all_in_4_out_2),
    .out_3(all_in_4_out_3), .out_4(all_in_4_out_4), .out_5(all_in_4_out_5), .out_6(all_in_4_out_6));
  _7_Segment_Display u_7_segment_display_5 (
    .g(all_in_4_out_3), .f(all_in_4_out_2), .a(all_in_4_out_1), .b(all_in_4_out_0), .e(all_in_4_out_4),
    .d(all_in_4_out_5), .c(all_in_4_out_6), .dp(undriven_3));

  // Notes on the sheet:
  //   reset 
  //   digital clock 
  //   1st minute: 0-9
  //   2nd 10's min. 0-5
  //   3rd hours 1-9,0-2
  //   4rth 0-2
  //   Michael Chrisco
  //   All inputs
  //   0-9 counter
  //   All inputs
  //   0-5 counter
  //   All inputs
  //   min 1s
  //   min 10's
  //   hours 
  //   10's of hours
  //   detect if over 12 then put 1 there
endmodule

module in_0 (
  input  S0,
  input  S1,
  input  S2,
  input  S3,
  output out_0
);

  wire and_1_out, and_2_out, and_3_out, and_4_out, and_5_out, and_6_out, not_2_out, not_3_out, not_4_out,
       or_1_out;

  // NOT_Gate not_1 has open pins: in=S1, out=open
  not not_2 (not_2_out, S0);
  not not_3 (not_3_out, S2);
  not not_4 (not_4_out, S3);
  and and_1 (and_1_out, not_2_out, S1);
  and and_2 (and_2_out, and_1_out, and_3_out);
  and and_3 (and_3_out, not_3_out, S3);
  and and_4 (and_4_out, not_2_out, S1);
  and and_5 (and_5_out, and_4_out, and_6_out);
  and and_6 (and_6_out, S2, not_4_out);
  or or_1 (or_1_out, and_2_out, and_5_out);
  not not_5 (out_0, or_1_out);
endmodule

module in_1 (
  input  S0,
  input  S1,
  input  S2,
  input  S3,
  output out_0
);

  wire and_1_out, and_2_out, and_3_out, and_4_out, not_1_out, not_2_out, not_3_out, not_4_out, or_1_out;

  not not_1 (not_1_out, S2);
  not not_2 (not_2_out, S0);
  not not_3 (not_3_out, S1);
  not not_4 (not_4_out, S3);
  and and_1 (and_1_out, not_2_out, S1);
  and and_2 (and_2_out, and_1_out, and_3_out);
  and and_3 (and_3_out, not_1_out, not_4_out);
  and and_4 (and_4_out, not_2_out, not_3_out, not_1_out, S3);
  or or_1 (or_1_out, and_2_out, and_4_out);
  not not_5 (out_0, or_1_out);
endmodule

module in_2 (
  input  S0,
  input  S1,
  input  S2,
  input  S3,
  output out_0
);

  wire and_1_out, and_2_out, and_3_out, and_4_out, not_1_out, not_2_out, not_3_out, not_4_out, or_1_out;

  not not_1 (not_1_out, S1);
  not not_2 (not_2_out, S0);
  not not_3 (not_3_out, S2);
  not not_4 (not_4_out, S3);
  and and_1 (and_1_out, not_2_out, not_1_out, not_3_out, S3);
  and and_2 (and_2_out, not_2_out, not_1_out, S2, not_4_out);
  and and_3 (and_3_out, not_2_out, not_1_out, S2, S3);
  and and_4 (and_4_out, not_2_out, S1, S2, S3);
  or or_1 (or_1_out, and_1_out, and_2_out, and_3_out, and_4_out);
  not not_5 (out_0, or_1_out);

  // Notes on the sheet:
  //   in 2
endmodule

module in_3 (
  input  S0,
  input  S1,
  input  S2,
  input  S3,
  output out_5
);

  wire and_1_out, and_2_out, and_3_out, not_1_out, not_2_out, not_3_out, not_4_out, or_1_out;

  not not_1 (not_1_out, S0);
  not not_2 (not_2_out, S1);
  not not_3 (not_3_out, S2);
  not not_4 (not_4_out, S3);
  and and_1 (and_1_out, not_1_out, not_2_out, not_3_out, not_4_out);
  and and_2 (and_2_out, not_1_out, not_2_out, not_3_out, S3);
  and and_3 (and_3_out, not_1_out, S1, S2, S3);
  or or_1 (or_1_out, and_1_out, and_2_out, and_3_out);
  not not_5 (out_5, or_1_out);
endmodule

module in_4 (
  input  S0,
  input  S1,
  input  S2,
  input  S3,
  output out_0
);

  wire and_1_out, and_2_out, and_3_out, and_4_out, not_1_out, not_2_out, not_3_out, not_4_out;

  not not_1 (not_1_out, S0);
  not not_2 (not_2_out, S2);
  not not_3 (not_3_out, S1);
  not not_4 (not_4_out, S3);
  and and_1 (and_1_out, not_1_out, not_3_out, not_2_out, not_4_out);
  and and_2 (and_2_out, not_1_out, not_3_out, S2, not_4_out);
  and and_3 (and_3_out, not_1_out, S1, S2, not_4_out);
  and and_4 (and_4_out, S0, not_3_out, not_2_out, not_4_out);
  or or_1 (out_0, and_1_out, and_2_out, and_3_out, and_4_out);
endmodule

module IN_5 (
  input  S0,
  input  S1,
  input  S2,
  input  S3,
  output out_5
);

  wire and_1_out, and_2_out, and_3_out, not_1_out, not_2_out, not_3_out, not_4_out, or_1_out;

  not not_1 (not_1_out, S0);
  not not_2 (not_2_out, S1);
  not not_3 (not_3_out, S3);
  not not_4 (not_4_out, S2);
  and and_1 (and_1_out, not_1_out, not_2_out, not_4_out, S3);
  and and_2 (and_2_out, not_1_out, S1, not_4_out, not_3_out);
  and and_3 (and_3_out, not_1_out, S1, S2, S3);
  or or_1 (or_1_out, and_1_out, and_2_out, and_3_out);
  not not_5 (out_5, or_1_out);
endmodule

module in_6 (
  input  S0,
  input  S1,
  input  S2,
  input  S3,
  output out_0
);

  wire and_1_out, not_1_out, not_2_out, not_3_out;

  not not_1 (not_1_out, S0);
  not not_2 (not_2_out, S1);
  not not_3 (not_3_out, S3);
  and and_1 (and_1_out, not_1_out, not_2_out, S2, not_3_out);
  not not_4 (out_0, and_1_out);
endmodule

module ALL_IN (
  input  S0,
  input  S1,
  input  S2,
  input  S3,
  output out_0,
  output out_1,
  output out_2,
  output out_3,
  output out_4,
  output out_5,
  output out_6
);

  in_0 in_0_1 (.S0(S0), .S1(S1), .S2(S2), .S3(S3), .out_0(out_0));
  in_1 in_1_1 (.S0(S0), .S1(S1), .S2(S2), .S3(S3), .out_0(out_1));
  in_2 in_2_1 (.S0(S0), .S1(S1), .S2(S2), .S3(S3), .out_0(out_2));
  in_3 in_3_1 (.S0(S0), .S1(S1), .S2(S2), .S3(S3), .out_5(out_3));
  in_4 in_4_1 (.S0(S0), .S1(S1), .S2(S2), .S3(S3), .out_0(out_4));
  IN_5 in_5_1 (.S0(S0), .S1(S1), .S2(S2), .S3(S3), .out_5(out_5));
  in_6 in_6_1 (.S0(S0), .S1(S1), .S2(S2), .S3(S3), .out_0(out_6));

  // Notes on the sheet:
  //   in 0
  //   in 1
  //   in 2
  //   in 3
  //   in 4
  //   in 5
  //   in 6
endmodule

module _0_5_counter (
  input  in_1,
  input  reset,
  output out_3,
  output out_4,
  output out_5,
  output out_6,
  output out_10
);

  wire and_1_out, clock_1_out, j_k_ff_1_qn, j_k_ff_2_qn, j_k_ff_3_qn, or_1_out;

  J_K_Flip_Flop #(.trigger("rising")) j_k_ff_1 (
    .J(1'b1), .clk(in_1), .K(1'b1), .Qn(j_k_ff_1_qn), .preset(or_1_out), .reset(or_1_out));  // open: Q, en
  not not_1 (out_4, j_k_ff_1_qn);
  not not_2 (out_5, j_k_ff_2_qn);
  J_K_Flip_Flop #(.trigger("rising")) j_k_ff_2 (
    .J(1'b1), .clk(j_k_ff_1_qn), .K(1'b1), .Qn(j_k_ff_2_qn), .reset(or_1_out));  // open: Q, preset, en
  not not_3 (out_6, j_k_ff_3_qn);
  J_K_Flip_Flop #(.trigger("rising")) j_k_ff_3 (
    .J(1'b1), .clk(j_k_ff_2_qn), .K(1'b1), .Qn(j_k_ff_3_qn), .reset(reset));  // open: Q, preset, en
  and and_1 (and_1_out, out_6, out_5, j_k_ff_1_qn);
  or or_1 (or_1_out, and_1_out, reset);
  Clock #(.highDuration(2), .lowDuration(2)) clock_1 (.out(clock_1_out));
  D_Flip_Flop #(.trigger("rising")) d_ff_1 (
    .clk(clock_1_out), .D(clock_1_out), .Q(out_10), .preset(and_1_out), .reset(and_1_out));  // open: Qn, en

  assign out_3 = 1'b0;

  // Notes on the sheet:
  //   0110
endmodule

module _0_9_counter (
  input  clock,
  input  in_2,
  output S0,
  output S1,
  output S2,
  output S3,
  output out_10
);

  wire and_1_out, controlled_buffer_1_out, controlled_buffer_2_out, j_k_ff_1_qn, j_k_ff_2_qn, j_k_ff_3_qn,
       j_k_ff_4_qn, not_2_out, or_1_out;

  not not_1 (S0, j_k_ff_1_qn);
  J_K_Flip_Flop #(.trigger("rising")) j_k_ff_1 (
    .J(1'b1), .clk(clock), .K(1'b1), .Qn(j_k_ff_1_qn), .reset(or_1_out));  // open: Q, preset, en
  not not_2 (not_2_out, in_2);
  not not_3 (S1, j_k_ff_2_qn);
  J_K_Flip_Flop #(.trigger("rising")) j_k_ff_2 (
    .J(1'b1), .clk(j_k_ff_1_qn), .K(1'b1), .Qn(j_k_ff_2_qn), .reset(or_1_out));  // open: Q, preset, en
  or or_1 (or_1_out, in_2, and_1_out);
  not not_4 (S2, j_k_ff_3_qn);
  J_K_Flip_Flop #(.trigger("rising")) j_k_ff_3 (
    .J(1'b1), .clk(controlled_buffer_2_out), .K(1'b1), .Qn(j_k_ff_3_qn), .preset(and_1_out), .reset(in_2));  // open: Q, en
  assign controlled_buffer_1_out = not_2_out ? j_k_ff_3_qn : 1'bz;  // Controlled_Buffer controlled_buffer_1
  assign controlled_buffer_2_out = not_2_out ? j_k_ff_2_qn : 1'bz;  // Controlled_Buffer controlled_buffer_2
  not not_5 (S3, j_k_ff_4_qn);
  J_K_Flip_Flop #(.trigger("rising")) j_k_ff_4 (
    .J(1'b1), .clk(controlled_buffer_1_out), .K(1'b1), .Qn(j_k_ff_4_qn), .preset(and_1_out), .en(in_2),
    .reset(in_2));  // open: Q
  and and_1 (and_1_out, S3, j_k_ff_3_qn, S1, j_k_ff_1_qn);
  D_Flip_Flop #(.trigger("rising")) d_ff_1 (
    .clk(clock), .D(clock), .Q(out_10), .preset(and_1_out), .reset(and_1_out));  // open: Qn, en

  // Notes on the sheet:
  //   reset made for "2" position
  //   a 0 to 9 counter with reset at 1001
  //   Michael Chrisco
endmodule

module _0_12_counter (
  input  in_1,
  output S0,
  output S1,
  output S2,
  output S3,
  output out_10
);

  wire and_1_out, j_k_ff_1_qn, j_k_ff_2_qn, j_k_ff_3_qn, j_k_ff_5_qn;

  not not_1 (S0, j_k_ff_1_qn);
  J_K_Flip_Flop #(.trigger("rising")) j_k_ff_1 (
    .J(1'b1), .clk(in_1), .K(1'b1), .Qn(j_k_ff_1_qn), .reset(and_1_out));  // open: Q, preset, en
  not not_2 (S1, j_k_ff_2_qn);
  J_K_Flip_Flop #(.trigger("rising")) j_k_ff_2 (
    .J(1'b1), .clk(j_k_ff_1_qn), .K(1'b1), .Qn(j_k_ff_2_qn), .reset(and_1_out));  // open: Q, preset, en
  not not_3 (S2, j_k_ff_3_qn);
  J_K_Flip_Flop #(.trigger("rising")) j_k_ff_3 (
    .J(1'b1), .clk(j_k_ff_2_qn), .K(1'b1), .Qn(j_k_ff_3_qn), .reset(and_1_out));  // open: Q, preset, en
  J_K_Flip_Flop #(.trigger("rising")) j_k_ff_4 (.J(1'b1), .clk(and_1_out), .K(1'b1));  // open: Q, Qn, preset, en, reset
  not not_4 (S3, j_k_ff_5_qn);
  J_K_Flip_Flop #(.trigger("rising")) j_k_ff_5 (
    .J(1'b1), .clk(j_k_ff_3_qn), .K(1'b1), .Qn(j_k_ff_5_qn), .preset(and_1_out));  // open: Q, en, reset
  J_K_Flip_Flop #(.trigger("rising")) j_k_ff_6 ();  // open: J, clk, K, Q, Qn, preset, en, reset
  and and_1 (and_1_out, S3, j_k_ff_3_qn, j_k_ff_2_qn, S0);
  J_K_Flip_Flop #(.trigger("rising")) j_k_ff_7 ();  // open: J, clk, K, Q, Qn, preset, en, reset

  // Notes on the sheet:
  //   Michael Chrisco
  //   a 0 to 12 counter with reset at 1100
endmodule

module _0_2_counter (
  input  in_1,
  output out_2,
  output out_3,
  output out_4,
  output out_5,
  output out_2_2
);

  wire and_1_out, clock_1_out, j_k_ff_1_qn, j_k_ff_2_q;

  not not_1 (out_5, j_k_ff_1_qn);
  J_K_Flip_Flop #(.trigger("rising")) j_k_ff_1 (
    .J(1'b1), .clk(in_1), .K(1'b1), .Qn(j_k_ff_1_qn), .reset(and_1_out));  // open: Q, preset, en
  J_K_Flip_Flop #(.trigger("rising")) j_k_ff_2 (
    .J(1'b1), .clk(j_k_ff_1_qn), .K(1'b1), .Q(j_k_ff_2_q), .reset(and_1_out));  // open: Qn, preset, en
  and and_1 (and_1_out, j_k_ff_2_q, j_k_ff_2_q);
  Clock #(.highDuration(1), .lowDuration(1)) clock_1 (.out(clock_1_out));
  not not_2 (out_2, 1'b1);
  D_Flip_Flop #(.trigger("rising")) d_ff_1 (
    .clk(clock_1_out), .D(clock_1_out), .Q(out_2_2), .preset(and_1_out), .reset(and_1_out));  // open: Qn, en

  assign out_3 = out_2;
  assign out_4 = out_2;
endmodule

module All_IN_0_12 (
  input  in_1,
  input  in_2,
  input  in_3,
  input  in_4,
  output out_0,
  output out_1,
  output out_2,
  output out_3,
  output out_4,
  output out_5,
  output out_6
);

  _3rd_in_0 u_3rd_in_0_1 (.S0(in_1), .S1(in_2), .S2(in_3), .S3(in_4), .out_0(out_0));
  _3rd_in_1 u_3rd_in_1_1 (.S0(in_1), .S1(in_2), .S2(in_3), .S3(in_4), .out_0(out_1));
  _3rd_in_2 u_3rd_in_2_1 (.in_1(in_1), .in_2(in_2), .in_3(in_3), .in_4(in_4), .out_5(out_2));
  _3rd_in_3 u_3rd_in_3_1 (.in_1(in_1), .in_2(in_2), .in_3(in_3), .in_4(in_4), .out_5(out_3));
  _3rd_in_4 u_3rd_in_4_1 (.in_1(in_1), .in_2(in_2), .in_3(in_3), .in_4(in_4), .out_5(out_4));
  _3rd_in_5 u_3rd_in_5_1 (.in_1(in_1), .in_2(in_2), .in_3(in_3), .in_4(in_4), .out_5(out_5));
  _3rd_in_6 u_3rd_in_6_1 (.in_1(in_1), .in_2(in_2), .in_3(in_3), .in_4(in_4), .out_5(out_6));
endmodule

module _3rd_in_0 (
  input  S0,
  input  S1,
  input  S2,
  input  S3,
  output out_0
);

  wire and_1_out, and_2_out, not_2_out, not_3_out, not_4_out, or_1_out;

  // NOT_Gate not_1 has open pins: in=S1, out=open
  not not_2 (not_2_out, S0);
  not not_3 (not_3_out, S2);
  not not_4 (not_4_out, S3);
  and and_1 (and_1_out, not_2_out, S1, not_3_out, not_4_out);
  and and_2 (and_2_out, not_2_out, S1, not_3_out, S3);
  or or_1 (or_1_out, and_1_out, and_2_out);
  not not_5 (out_0, or_1_out);
endmodule

module _3rd_in_1 (
  input  S0,
  input  S1,
  input  S2,
  input  S3,
  output out_0
);

  wire and_1_out, and_2_out, and_3_out, not_1_out, not_2_out, not_3_out, not_4_out, or_1_out;

  not not_1 (not_1_out, S1);
  not not_2 (not_2_out, S0);
  not not_3 (not_3_out, S2);
  not not_4 (not_4_out, S3);
  and and_1 (and_1_out, not_2_out, not_2_out, not_1_out, not_3_out, not_4_out);
  and and_2 (and_2_out, not_2_out, not_1_out, S2, S3);
  and and_3 (and_3_out, S0, not_1_out, S2, not_4_out);
  or or_1 (or_1_out, and_1_out, and_2_out, and_3_out);
  not not_5 (out_0, or_1_out);
endmodule

module _3rd_in_2 (
  input  in_1,
  input  in_2,
  input  in_3,
  input  in_4,
  output out_5
);

  wire and_1_out, and_2_out, and_3_out, and_4_out, and_5_out, and_6_out, not_1_out, not_2_out, not_3_out,
       not_4_out, or_1_out;

  not not_1 (not_1_out, in_1);
  not not_2 (not_2_out, in_2);
  not not_3 (not_3_out, in_3);
  and and_1 (and_1_out, not_1_out, not_2_out, not_3_out, not_4_out);
  and and_2 (and_2_out, not_1_out, not_2_out, not_3_out, in_4);
  and and_3 (and_3_out, not_1_out, not_2_out, in_3, not_4_out);
  and and_4 (and_4_out, not_1_out, in_2, in_3, not_4_out);
  and and_5 (and_5_out, in_1, not_2_out, in_3, not_4_out);
  and and_6 (and_6_out, in_1, not_2_out, in_3, in_4);
  not not_4 (not_4_out, in_4);
  or or_1 (or_1_out, and_1_out, and_2_out, and_3_out, and_4_out, and_5_out, and_6_out);
  not not_5 (out_5, or_1_out);
endmodule

module _3rd_in_3 (
  input  in_1,
  input  in_2,
  input  in_3,
  input  in_4,
  output out_5
);

  wire and_1_out, and_2_out, and_3_out, and_4_out, not_1_out, not_2_out, not_3_out, not_4_out, or_1_out;

  not not_1 (not_1_out, in_1);
  not not_2 (not_2_out, in_2);
  not not_3 (not_3_out, in_3);
  not not_4 (not_4_out, in_4);
  and and_1 (and_1_out, not_1_out, not_2_out, not_3_out, not_4_out);
  and and_2 (and_2_out, not_1_out, in_2, in_3, not_4_out);
  and and_3 (and_3_out, in_1, not_2_out, in_3, not_4_out);
  and and_4 (and_4_out, in_1, not_2_out, not_3_out, in_4);
  or or_1 (or_1_out, and_1_out, and_2_out, and_3_out, and_4_out);
  not not_5 (out_5, or_1_out);
endmodule

module _3rd_in_4 (
  input  in_1,
  input  in_2,
  input  in_3,
  input  in_4,
  output out_5
);

  wire and_1_out, and_2_out, and_3_out, and_4_out, and_5_out, not_1_out, not_2_out, not_3_out;

  not not_1 (not_1_out, in_1);
  not not_2 (not_2_out, in_2);
  not not_3 (not_3_out, in_3);
  // NOT_Gate not_4 has open pins: in=in_4, out=open
  and and_1 (and_1_out, not_1_out, not_2_out, not_3_out, in_4);
  and and_2 (and_2_out, not_1_out, in_2, not_3_out, in_4);
  and and_3 (and_3_out, not_1_out, in_2, in_3, in_4);
  and and_4 (and_4_out, in_1, not_2_out, not_3_out, in_4);
  and and_5 (and_5_out, in_1, not_2_out, in_3, in_3, in_4);
  or or_1 (out_5, and_1_out, and_2_out, and_5_out, and_3_out, and_4_out);
endmodule

module _3rd_in_5 (
  input  in_1,
  input  in_2,
  input  in_3,
  input  in_4,
  output out_5
);

  wire and_1_out, and_2_out, and_3_out, and_4_out, not_1_out, not_2_out, not_3_out, not_4_out, or_1_out;

  not not_1 (not_1_out, in_1);
  not not_2 (not_2_out, in_2);
  not not_3 (not_3_out, in_4);
  not not_4 (not_4_out, in_3);
  and and_1 (and_1_out, not_1_out, not_2_out, not_4_out, not_3_out);
  and and_2 (and_2_out, not_1_out, not_2_out, in_3, in_4);
  and and_3 (and_3_out, not_1_out, in_2, in_3, not_3_out);
  and and_4 (and_4_out, in_1, not_2_out, in_3, not_3_out);
  or or_1 (or_1_out, and_1_out, and_2_out, and_3_out, and_4_out);
  not not_5 (out_5, or_1_out);
endmodule

module new_0_12_counter (
  input  clock,
  output S0,
  output S1,
  output S2,
  output S3,
  output last_place_digit
);

  wire and_1_out, and_2_out, j_k_ff_2_q, j_k_ff_2_qn, j_k_ff_3_q, n1_9_counter_1_out_10, not_1_out, or_1_out,
       or_2_out;

  J_K_Flip_Flop #(.trigger("rising")) j_k_ff_1 (
    .J(1'b1), .clk(not_1_out), .K(1'b1), .Q(last_place_digit), .reset(or_2_out));  // open: Qn, preset, en
  or or_1 (or_1_out, or_2_out, and_2_out);
  not not_1 (not_1_out, n1_9_counter_1_out_10);
  buf and_1 (and_1_out, last_place_digit);  // AND_Gate
  _1_9_counter u_1_9_counter_1 (
    .clock(clock), .reset_to_1(or_1_out), .out_10(n1_9_counter_1_out_10), .S0(S0), .S1(S1), .S2(S2), .S3(S3));  // open: reset_to_0
  J_K_Flip_Flop #(.trigger("rising")) j_k_ff_2 (
    .J(1'b1), .clk(and_1_out), .K(1'b1), .Q(j_k_ff_2_q), .Qn(j_k_ff_2_qn), .reset(or_2_out));  // open: preset, en
  J_K_Flip_Flop #(.trigger("rising")) j_k_ff_3 (
    .J(1'b1), .clk(j_k_ff_2_qn), .K(1'b1), .Q(j_k_ff_3_q), .reset(or_2_out));  // open: Qn, preset, en
  and and_2 (and_2_out, last_place_digit, j_k_ff_2_q, S0, S1);
  or or_2 (or_2_out, and_2_out, j_k_ff_3_q);
endmodule

module _3rd_in_6 (
  input  in_1,
  input  in_2,
  input  in_3,
  input  in_4,
  output out_5
);

  wire and_1_out, and_2_out, not_1_out, not_2_out, not_3_out, or_1_out;

  not not_1 (not_1_out, in_2);
  not not_2 (not_2_out, in_1);
  not not_3 (not_3_out, in_3);
  and and_1 (and_1_out, not_2_out, not_1_out, not_3_out, in_4);
  and and_2 (and_2_out, in_1, not_1_out, in_3, in_4);
  or or_1 (or_1_out, and_1_out, and_2_out);
  not not_4 (out_5, or_1_out);
endmodule

module _1_9_counter (
  input  clock,
  input  reset_to_1,
  input  reset_to_0,
  output S0,
  output S1,
  output S2,
  output S3,
  output out_10
);

  wire and_1_out, controlled_buffer_1_out, j_k_ff_1_qn, j_k_ff_2_qn, j_k_ff_3_qn, j_k_ff_4_qn, not_2_out,
       or_1_out, or_2_out;

  not not_1 (S0, j_k_ff_1_qn);
  J_K_Flip_Flop #(.trigger("rising")) j_k_ff_1 (
    .J(1'b1), .clk(clock), .K(1'b1), .Qn(j_k_ff_1_qn), .preset(reset_to_1));  // open: Q, en, reset
  or or_1 (or_1_out, reset_to_1, reset_to_0);
  not not_2 (not_2_out, or_1_out);
  not not_3 (S1, j_k_ff_2_qn);
  J_K_Flip_Flop #(.trigger("rising")) j_k_ff_2 (
    .J(1'b1), .clk(j_k_ff_1_qn), .K(1'b1), .Qn(j_k_ff_2_qn), .reset(or_2_out));  // open: Q, preset, en
  or or_2 (or_2_out, or_1_out, and_1_out);
  not not_4 (S2, j_k_ff_3_qn);
  J_K_Flip_Flop #(.trigger("rising")) j_k_ff_3 (
    .J(1'b1), .clk(controlled_buffer_1_out), .K(1'b1), .Qn(j_k_ff_3_qn), .preset(and_1_out), .reset(or_1_out));  // open: Q, en
  assign controlled_buffer_1_out = not_2_out ? j_k_ff_2_qn : 1'bz;  // Controlled_Buffer controlled_buffer_1
  not not_5 (S3, j_k_ff_4_qn);
  J_K_Flip_Flop #(.trigger("rising")) j_k_ff_4 (
    .J(1'b1), .clk(j_k_ff_3_qn), .K(1'b1), .Qn(j_k_ff_4_qn), .preset(and_1_out), .reset(or_1_out));  // open: Q, en
  and and_1 (and_1_out, S3, j_k_ff_3_qn, S1, j_k_ff_1_qn);
  D_Flip_Flop #(.trigger("rising")) d_ff_1 (
    .clk(clock), .D(clock), .Q(out_10), .preset(and_1_out), .reset(and_1_out));  // open: Qn, en

  // Notes on the sheet:
  //   reset made for "2" position
  //   a 1 to 9 counter with reset at 1001
  //   Michael Chrisco
endmodule

module ALL_INv2 (
  input  S0,
  input  S1,
  input  S2,
  input  S3,
  output out0,
  output out1,
  output out2,
  output out3,
  output out4,
  output out5,
  output out6
);

  wire and_1_out, and_2_out, and_3_out, and_4_out, and_5_out, and_6_out, and_7_out, and_8_out, and_9_out,
       and_10_out, and_11_out, and_12_out, and_13_out, and_14_out, and_15_out, and_16_out, not_1_out,
       not_2_out, not_3_out, not_4_out, not_5_out, not_6_out, not_7_out, not_8_out, not_9_out, not_10_out,
       not_11_out, not_12_out, not_13_out, not_14_out, not_15_out, not_16_out, not_17_out, not_18_out,
       not_19_out, not_20_out, not_21_out, not_22_out, not_23_out;

  not not_1 (not_1_out, S1);
  not not_2 (not_2_out, S2);
  and and_1 (and_1_out, not_2_out, not_3_out);
  not not_3 (not_3_out, S3);
  and and_2 (and_2_out, S2, S3);
  not not_4 (not_4_out, S1);
  and and_3 (and_3_out, not_4_out, not_5_out);
  not not_5 (not_5_out, S3);
  and and_4 (and_4_out, S1, S3);
  not not_6 (not_6_out, S2);
  and and_5 (and_5_out, not_6_out, not_7_out);
  not not_7 (not_7_out, S3);
  and and_6 (and_6_out, S1, not_8_out);
  not not_8 (not_8_out, S2);
  and and_7 (and_7_out, S1, not_9_out);
  not not_9 (not_9_out, S3);
  not not_10 (not_10_out, S1);
  and and_8 (and_8_out, not_10_out, S2);
  and and_9 (and_9_out, S2, not_11_out);
  not not_11 (not_11_out, S3);
  and and_10 (and_10_out, S1, not_12_out);
  not not_12 (not_12_out, S2);
  not not_13 (not_13_out, S1);
  and and_11 (and_11_out, not_13_out, not_14_out, not_15_out);
  not not_14 (not_14_out, S2);
  not not_15 (not_15_out, S3);
  not not_16 (not_16_out, S0);
  and and_12 (and_12_out, not_16_out, S2, not_17_out);
  not not_17 (not_17_out, S3);
  not not_18 (not_18_out, S1);
  and and_13 (and_13_out, not_18_out, not_19_out);
  not not_19 (not_19_out, S3);
  not not_20 (not_20_out, S1);
  and and_14 (and_14_out, not_20_out, S2);
  and and_15 (and_15_out, S2, not_21_out);
  not not_21 (not_21_out, S3);
  and and_16 (and_16_out, S1, not_22_out, S3);
  not not_22 (not_22_out, S2);
  not not_23 (not_23_out, S2);
  or or_1 (out0, not_1_out, and_1_out, and_2_out, S0);
  or or_2 (out1, and_3_out, S2, and_4_out, S0);
  or or_3 (out2, and_5_out, and_6_out, and_7_out, S0);
  or or_4 (out3, and_8_out, and_9_out, and_10_out, S0);
  or or_5 (out4, and_11_out, and_12_out);
  or or_6 (out5, and_13_out, and_14_out, and_15_out, and_16_out, S0);
  or or_7 (out6, not_23_out, S3, S1, S0);
endmodule
