// Logisim project calc_basic.circ as structural Verilog
module main (
  output S0,
  output S1,
  output S2,
  output S3,
  output out_10
);

  wire and_1_out, clock_1_out, j_k_ff_1_qn, j_k_ff_2_qn, j_k_ff_3_qn, j_k_ff_4_qn;

  Clock #(.highDuration(1), .lowDuration(1)) clock_1 (.out(clock_1_out));
  not not_1 (S0, j_k_ff_1_qn);
  J_K_Flip_Flop #(.trigger("rising")) j_k_ff_1 (
    .J(1'b1), .clk(clock_1_out), .K(1'b1), .Qn(j_k_ff_1_qn), .preset(and_1_out));  // open: Q, en, reset
  not not_2 (S1, j_k_ff_2_qn);
  J_K_Flip_Flop #(.trigger("rising")) j_k_ff_2 (
    .J(1'b1), .clk(j_k_ff_1_qn), .K(1'b1), .Qn(j_k_ff_2_qn), .preset(and_1_out));  // open: Q, en, reset
  not not_3 (S2, j_k_ff_3_qn);
  J_K_Flip_Flop #(.trigger("rising")) j_k_ff_3 (
    .J(1'b1), .clk(j_k_ff_2_qn), .K(1'b1), .Qn(j_k_ff_3_qn), .preset(and_1_out));  // open: Q, en, reset
  not not_4 (S3, j_k_ff_4_qn);
  J_K_Flip_Flop #(.trigger("rising")) j_k_ff_4 (
    .J(1'b1), .clk(j_k_ff_3_qn), .K(1'b1), .Qn(j_k_ff_4_qn), .preset(and_1_out));  // open: Q, en, reset
  and and_1 (and_1_out, S3, j_k_ff_3_qn, j_k_ff_2_qn, S0);
  D_Flip_Flop #(.trigger("rising")) d_ff_1 (
    .clk(clock_1_out), .D(clock_1_out), .Q(out_10), .preset(and_1_out), .reset(and_1_out));  // open: Qn, en

  // Notes on the sheet:
  //   a 0 to 9 counter with reset at 1001
  //   Michael Chrisco
endmodule

module out_0101 (
  input  cpy_signal,
  output out_0101
);

  wire and_1_out, clock_1_out, controlled_buffer_1_out, j_k_ff_1_q, j_k_ff_1_qn, j_k_ff_2_q, nand_1_out;

  assign controlled_buffer_1_out = nand_1_out ? clock_1_out : 1'bz;  // Controlled_Buffer controlled_buffer_1
  Clock #(.highDuration(1), .lowDuration(1)) clock_1 (.out(clock_1_out));
  J_K_Flip_Flop #(.trigger("rising")) j_k_ff_1 (
    .J(1'b1), .clk(and_1_out), .K(1'b1), .Q(j_k_ff_1_q), .Qn(j_k_ff_1_qn));  // open: preset, en, reset
  and and_1 (and_1_out, cpy_signal, controlled_buffer_1_out);
  nand nand_1 (nand_1_out, j_k_ff_2_q, j_k_ff_1_q);
  not not_1 (out_0101, j_k_ff_1_q);
  J_K_Flip_Flop #(.trigger("rising")) j_k_ff_2 (
    .J(1'b1), .clk(j_k_ff_1_qn), .K(1'b1), .Q(j_k_ff_2_q));  // open: Qn, preset, en, reset
endmodule

module memory_4_bit (
  input  store_1,
  input  store_2,
  input  store_4,
  input  store_8,
  input  reset,
  input  cpy
);

  wire controlled_buffer_1_out, controlled_buffer_2_out, controlled_buffer_3_out, controlled_buffer_4_out,
       j_k_ff_1_qn, j_k_ff_3_qn, j_k_ff_5_qn, j_k_ff_7_qn, or_1_out, or_2_out, or_3_out, or_4_out,
       out_0101_1_out_0101;

  out_0101 out_0101_1 (.cpy_signal(cpy), .out_0101(out_0101_1_out_0101));
  J_K_Flip_Flop #(.trigger("rising")) j_k_ff_1 (
    .J(1'b1), .clk(or_1_out), .K(1'b1), .Qn(j_k_ff_1_qn), .reset(reset));  // open: Q, preset, en
  assign controlled_buffer_1_out = cpy ? j_k_ff_1_qn : 1'bz;  // Controlled_Buffer controlled_buffer_1
  J_K_Flip_Flop #(.trigger("rising")) j_k_ff_2 (
    .J(1'b1), .clk(controlled_buffer_1_out), .K(1'b1));  // open: Q, Qn, preset, en, reset
  or or_1 (or_1_out, out_0101_1_out_0101, store_1);
  J_K_Flip_Flop #(.trigger("rising")) j_k_ff_3 (
    .J(1'b1), .clk(or_2_out), .K(1'b1), .Qn(j_k_ff_3_qn), .reset(reset));  // open: Q, preset, en
  J_K_Flip_Flop #(.trigger("rising")) j_k_ff_4 (
    .J(1'b1), .clk(controlled_buffer_2_out), .K(1'b1));  // open: Q, Qn, preset, en, reset
  or or_2 (or_2_out, out_0101_1_out_0101, store_2);
  assign controlled_buffer_2_out = cpy ? j_k_ff_3_qn : 1'bz;  // Controlled_Buffer controlled_buffer_2
  or or_3 (or_3_out, out_0101_1_out_0101, store_4);
  J_K_Flip_Flop #(.trigger("rising")) j_k_ff_5 (
    .J(1'b1), .clk(or_3_out), .K(1'b1), .Qn(j_k_ff_5_qn), .reset(reset));  // open: Q, preset, en
  assign controlled_buffer_3_out = cpy ? j_k_ff_5_qn : 1'bz;  // Controlled_Buffer controlled_buffer_3
  J_K_Flip_Flop #(.trigger("rising")) j_k_ff_6 (
    .J(1'b1), .clk(controlled_buffer_3_out), .K(1'b1));  // open: Q, Qn, preset, en, reset
  or or_4 (or_4_out, out_0101_1_out_0101, store_8);
  J_K_Flip_Flop #(.trigger("rising")) j_k_ff_7 (
    .J(1'b1), .clk(or_4_out), .K(1'b1), .Qn(j_k_ff_7_qn), .reset(reset));  // open: Q, preset, en
  assign controlled_buffer_4_out = cpy ? j_k_ff_7_qn : 1'bz;  // Controlled_Buffer controlled_buffer_4
  J_K_Flip_Flop #(.trigger("rising")) j_k_ff_8 (
    .J(1'b1), .clk(controlled_buffer_4_out), .K(1'b1));  // open: Q, Qn, preset, en, reset

  // Notes on the sheet:
  //   cpy: first enable copy, then "storeage 1-8" press twice 
  //   testing 4-bit RAM cpy function
  //   4 bit RAM
endmodule

module _1_or_0_states_need_to_redo (
  input  first_gate,
  input  second_gate,
  input  ENABLE,
  output out_4,
  output pulser_1
);

  wire and_1_out, and_2_out, and_3_out, controlled_buffer_1_out, not_1_out, not_2_out, or_1_out, or_2_out;

  not not_1 (not_1_out, first_gate);
  and and_1 (and_1_out, not_1_out, second_gate);
  and and_2 (and_2_out, first_gate, not_2_out);
  not not_2 (not_2_out, second_gate);
  or or_1 (or_1_out, first_gate, second_gate);
  and and_3 (and_3_out, or_2_out, ENABLE);
  or or_2 (or_2_out, and_1_out, and_2_out);
  assign controlled_buffer_1_out = and_3_out ? or_1_out : 1'bz;  // Controlled_Buffer controlled_buffer_1
  _1_pulser u_1_pulser_1 (.cpy_signal(controlled_buffer_1_out), .out_01(out_4));

  assign pulser_1 = out_4;

  // Notes on the sheet:
  //   If they are different, then 
endmodule

module _1_pulser (
  input  cpy_signal,
  output out_01
);

  wire and_1_out, clock_1_out, controlled_buffer_1_out, j_k_ff_1_q, not_1_out;

  Clock #(.highDuration(1), .lowDuration(1)) clock_1 (.out(clock_1_out));
  assign controlled_buffer_1_out = not_1_out ? clock_1_out : 1'bz;  // Controlled_Buffer controlled_buffer_1
  J_K_Flip_Flop #(.trigger("rising")) j_k_ff_1 (
    .J(1'b1), .clk(and_1_out), .K(1'b1), .Q(j_k_ff_1_q));  // open: Qn, preset, en, reset
  and and_1 (and_1_out, cpy_signal, controlled_buffer_1_out);
  not not_1 (not_1_out, j_k_ff_1_q);
  not not_2 (out_01, j_k_ff_1_q);

  // Notes on the sheet:
  //   1 pulser
  //   Michael Chrisco
endmodule

module _2_bit_tes_not_working (
  input  in_1,
  input  in_2,
  input  in_3,
  output out_4,
  output out_5
);

  wire n1_bit_1_cpy_nxt, n1_bit_1_cpy_reset, or_1_out, or_2_out;

  _1_bit u_1_bit_1 (
    .reset(in_2), .cpy(in_3), .add_1(in_1), .current_state(out_4), .cpy_nxt(n1_bit_1_cpy_nxt),
    .ther_bit_state(out_5), .cpy_reset(n1_bit_1_cpy_reset));
  or or_1 (or_1_out, in_2, n1_bit_1_cpy_reset);
  or or_2 (or_2_out, n1_bit_1_cpy_nxt, in_1);
  _1_bit u_1_bit_2 (
    .reset(or_1_out), .cpy(in_3), .add_1(or_2_out), .current_state(out_5), .ther_bit_state(out_4));  // open: cpy_nxt, cpy_reset
endmodule

module _1_bit (
  input  add_1,
  input  ther_bit_state,
  input  reset,
  input  cpy,
  output cpy_nxt,
  output cpy_reset,
  output current_state
);

  wire or_1_out, out_0101_1_out_0101;

  out_0101 out_0101_1 (.cpy_signal(cpy), .out_0101(out_0101_1_out_0101));
  or or_1 (or_1_out, out_0101_1_out_0101, add_1);
  J_K_Flip_Flop #(.trigger("rising")) j_k_ff_1 (
    .J(1'b1), .clk(or_1_out), .K(1'b1), .Q(current_state), .reset(reset));  // open: Qn, preset, en
  _1_pulser u_1_pulser_1 (.cpy_signal(cpy), .out_01(cpy_reset));
  _1_or_0_states_need_to_redo u_1_or_0_states_need_to_redo_1 (
    .first_gate(current_state), .second_gate(ther_bit_state), .out_4(cpy_nxt), .ENABLE(cpy));  // open: pulser_1

  // Notes on the sheet:
  //   00 has problem
endmodule

module compare_1_bit_with_another (
  input  first_gate,
  input  second_gate,
  output out
);

  wire and_1_out, and_2_out, not_1_out, not_2_out;

  not not_1 (not_1_out, first_gate);
  not not_2 (not_2_out, second_gate);
  and and_1 (and_1_out, not_1_out, second_gate);
  and and_2 (and_2_out, first_gate, not_2_out);
  or or_1 (out, and_1_out, and_2_out);
endmodule
