// Logisim project comparator.circ as structural Verilog: 3 circuits, main circuit 4 bit comparator
module _1_bit_comparator (
  input  Xi,
  input  Yi,
  output X_Y,
  output X_Y_2,
  output X_Y_3
);

  wire not_1_out, not_2_out;

  not not_1 (not_1_out, Xi);
  not not_2 (not_2_out, Yi);
  and and_1 (X_Y, Xi, not_2_out);
  xnor xnor_1 (X_Y_2, Xi, Yi);
  and and_2 (X_Y_3, not_1_out, Yi);
endmodule

module _1_bit_comparitor_w__proagated_inputs (
  input  Xi,
  input  Yi,
  input  X_Yin,
  input  X_Yin_2,
  input  X_Yin_3,
  output X_Yout,
  output X_Yout_2,
  output X_Yout_3
);

  wire and_1_out, and_2_out, not_1_out, not_2_out, xnor_1_out;

  not not_1 (not_1_out, Yi);
  not not_2 (not_2_out, Xi);
  and and_1 (and_1_out, Xi, not_1_out, X_Yin_2);
  xnor xnor_1 (xnor_1_out, Xi, Yi);
  and and_2 (and_2_out, X_Yin_2, not_2_out, Yi);
  or or_1 (X_Yout, and_1_out, X_Yin);
  and and_3 (X_Yout_2, xnor_1_out, X_Yin_2);
  or or_2 (X_Yout_3, and_2_out, X_Yin_3);
endmodule

module _4_bit_comparator (
  input  Y0,
  input  X0,
  input  Y1,
  input  X1,
  input  Y2,
  input  X2,
  input  Y3,
  input  X3,
  output X_Y,
  output X_Y_2,
  output X_Y_3
);

  wire n1_bit_comparitor_w_proagated_inputs_1_x_yout, n1_bit_comparitor_w_proagated_inputs_1_x_yout_2,
       n1_bit_comparitor_w_proagated_inputs_1_x_yout_3, n1_bit_comparitor_w_proagated_inputs_2_x_yout,
       n1_bit_comparitor_w_proagated_inputs_2_x_yout_2, n1_bit_comparitor_w_proagated_inputs_2_x_yout_3,
       n1_bit_comparitor_w_proagated_inputs_3_x_yout, n1_bit_comparitor_w_proagated_inputs_3_x_yout_2,
       n1_bit_comparitor_w_proagated_inputs_3_x_yout_3;

  _1_bit_comparitor_w__proagated_inputs u_1_bit_comparitor_w_proagated_inputs_1 (
    .X_Yin(1'b0), .X_Yin_2(1'b1), .X_Yin_3(1'b0), .Xi(Y0), .Yi(X0),
    .X_Yout(n1_bit_comparitor_w_proagated_inputs_1_x_yout),
    .X_Yout_2(n1_bit_comparitor_w_proagated_inputs_1_x_yout_2),
    .X_Yout_3(n1_bit_comparitor_w_proagated_inputs_1_x_yout_3));
  _1_bit_comparitor_w__proagated_inputs u_1_bit_comparitor_w_proagated_inputs_2 (
    .X_Yin(n1_bit_comparitor_w_proagated_inputs_1_x_yout),
    .X_Yin_2(n1_bit_comparitor_w_proagated_inputs_1_x_yout_2),
    .X_Yin_3(n1_bit_comparitor_w_proagated_inputs_1_x_yout_3), .Xi(Y1), .Yi(X1),
    .X_Yout(n1_bit_comparitor_w_proagated_inputs_2_x_yout),
    .X_Yout_2(n1_bit_comparitor_w_proagated_inputs_2_x_yout_2),
    .X_Yout_3(n1_bit_comparitor_w_proagated_inputs_2_x_yout_3));
  _1_bit_comparitor_w__proagated_inputs u_1_bit_comparitor_w_proagated_inputs_3 (
    .X_Yin(n1_bit_comparitor_w_proagated_inputs_2_x_yout),
    .X_Yin_2(n1_bit_comparitor_w_proagated_inputs_2_x_yout_2),
    .X_Yin_3(n1_bit_comparitor_w_proagated_inputs_2_x_yout_3), .Xi(Y2), .Yi(X2),
    .X_Yout(n1_bit_comparitor_w_proagated_inputs_3_x_yout),
    .X_Yout_2(n1_bit_comparitor_w_proagated_inputs_3_x_yout_2),
    .X_Yout_3(n1_bit_comparitor_w_proagated_inputs_3_x_yout_3));
  _1_bit_comparitor_w__proagated_inputs u_1_bit_comparitor_w_proagated_inputs_4 (
    .X_Yin(n1_bit_comparitor_w_proagated_inputs_3_x_yout),
    .X_Yin_2(n1_bit_comparitor_w_proagated_inputs_3_x_yout_2),
    .X_Yin_3(n1_bit_comparitor_w_proagated_inputs_3_x_yout_3), .Xi(Y3), .Yi(X3), .X_Yout(X_Y_3),
    .X_Yout_2(X_Y_2), .X_Yout_3(X_Y));
endmodule
