// Logisim project plsers.circ as structural Verilog: 9 circuits, main circuit main
module main (
  input  in_1,
  input  in_2
);

  wire n16_pulser_1__2_pulse;

  _16_pulser u_16_pulser_1 (.in_1(in_1), ._2_pulse(n16_pulser_1__2_pulse));
  memory_module_4_bit memory_module_4_bit_1 ();  // open: reset, cpy, s0, s1, s2, s3, S0_out, S1_out, S2_out, S3_out, cpy_0, cpy_1, cpy_2, cpy_3, reset_signal
  memory_module_4_bit memory_module_4_bit_2 ();  // open: reset, cpy, s0, s1, s2, s3, S0_out, S1_out, S2_out, S3_out, cpy_0, cpy_1, cpy_2, cpy_3, reset_signal

  // Notes on the sheet:
  //   add 1
  //   8 pulsers
endmodule

module _1_pulser (
  input  cpy_signal,
  output _1_pulse
);

  wire and_1_out, clock_1_out, controlled_buffer_1_out, j_k_ff_1_q, not_1_out;

  Clock #(.highDuration(1), .lowDuration(1)) clock_1 (.out(clock_1_out));
  assign controlled_buffer_1_out = not_1_out ? clock_1_out : 1'bz;  // Controlled_Buffer controlled_buffer_1
  J_K_Flip_Flop #(.trigger("rising")) j_k_ff_1 (
    .J(1'b1), .clk(and_1_out), .K(1'b1), .Q(j_k_ff_1_q));  // open: Qn, preset, en, reset
  and and_1 (and_1_out, cpy_signal, controlled_buffer_1_out);
  not not_1 (not_1_out, j_k_ff_1_q);
  not not_2 (_1_pulse, j_k_ff_1_q);

  // Notes on the sheet:
  //   1 pulser
  //   Michael Chrisco
endmodule

module _2_pulsers (
  input  pulse_input,
  output _2_pulse
);

  wire and_1_out, clock_1_out, controlled_buffer_1_out, j_k_ff_1_q, j_k_ff_1_qn, j_k_ff_2_q, nand_1_out;

  Clock #(.highDuration(1), .lowDuration(1)) clock_1 (.out(clock_1_out));
  assign controlled_buffer_1_out = nand_1_out ? clock_1_out : 1'bz;  // Controlled_Buffer controlled_buffer_1
  J_K_Flip_Flop #(.trigger("rising")) j_k_ff_1 (
    .J(1'b1), .clk(and_1_out), .K(1'b1), .Q(j_k_ff_1_q), .Qn(j_k_ff_1_qn));  // open: preset, en, reset
  and and_1 (and_1_out, pulse_input, controlled_buffer_1_out);
  nand nand_1 (nand_1_out, j_k_ff_2_q, j_k_ff_1_q);
  not not_1 (_2_pulse, j_k_ff_1_q);
  J_K_Flip_Flop #(.trigger("rising")) j_k_ff_2 (
    .J(1'b1), .clk(j_k_ff_1_qn), .K(1'b1), .Q(j_k_ff_2_q));  // open: Qn, preset, en, reset
endmodule

module _4_pulsers (
  input  in_1,
  output _2_pulse
);

  wire and_1_out, clock_1_out, controlled_buffer_1_out, j_k_ff_1_q, j_k_ff_1_qn, j_k_ff_2_q, j_k_ff_2_qn,
       j_k_ff_3_q, nand_1_out;

  assign controlled_buffer_1_out = nand_1_out ? clock_1_out : 1'bz;  // Controlled_Buffer controlled_buffer_1
  Clock #(.highDuration(1), .lowDuration(1)) clock_1 (.out(clock_1_out));
  and and_1 (and_1_out, in_1, controlled_buffer_1_out);
  J_K_Flip_Flop #(.trigger("rising")) j_k_ff_1 (
    .J(1'b1), .clk(and_1_out), .K(1'b1), .Q(j_k_ff_1_q), .Qn(j_k_ff_1_qn));  // open: preset, en, reset
  not not_1 (_2_pulse, j_k_ff_1_q);
  J_K_Flip_Flop #(.trigger("rising")) j_k_ff_2 (
    .J(1'b1), .clk(j_k_ff_1_qn), .K(1'b1), .Q(j_k_ff_2_q), .Qn(j_k_ff_2_qn));  // open: preset, en, reset
  nand nand_1 (nand_1_out, j_k_ff_1_q, j_k_ff_2_q, j_k_ff_3_q);
  J_K_Flip_Flop #(.trigger("rising")) j_k_ff_3 (
    .J(1'b1), .clk(j_k_ff_2_qn), .K(1'b1), .Q(j_k_ff_3_q));  // open: Qn, preset, en, reset
endmodule

module _8_pulsers (
  input  in_1,
  output _2_pulse
);

  wire and_1_out, clock_1_out, controlled_buffer_1_out, j_k_ff_1_q, j_k_ff_1_qn, j_k_ff_2_q, j_k_ff_2_qn,
       j_k_ff_3_q, j_k_ff_3_qn, j_k_ff_4_q, nand_1_out;

  assign controlled_buffer_1_out = nand_1_out ? clock_1_out : 1'bz;  // Controlled_Buffer controlled_buffer_1
  Clock #(.highDuration(1), .lowDuration(1)) clock_1 (.out(clock_1_out));
  and and_1 (and_1_out, in_1, controlled_buffer_1_out);
  J_K_Flip_Flop #(.trigger("rising")) j_k_ff_1 (
    .J(1'b1), .clk(and_1_out), .K(1'b1), .Q(j_k_ff_1_q), .Qn(j_k_ff_1_qn));  // open: preset, en, reset
  not not_1 (_2_pulse, j_k_ff_1_q);
  J_K_Flip_Flop #(.trigger("rising")) j_k_ff_2 (
    .J(1'b1), .clk(j_k_ff_1_qn), .K(1'b1), .Q(j_k_ff_2_q), .Qn(j_k_ff_2_qn));  // open: preset, en, reset
  nand nand_1 (nand_1_out, j_k_ff_1_q, j_k_ff_2_q, j_k_ff_3_q, j_k_ff_4_q);
  J_K_Flip_Flop #(.trigger("rising")) j_k_ff_3 (
    .J(1'b1), .clk(j_k_ff_2_qn), .K(1'b1), .Q(j_k_ff_3_q), .Qn(j_k_ff_3_qn));  // open: preset, en, reset
  J_K_Flip_Flop #(.trigger("rising")) j_k_ff_4 (
    .J(1'b1), .clk(j_k_ff_3_qn), .K(1'b1), .Q(j_k_ff_4_q));  // open: Qn, preset, en, reset
endmodule

module _16_pulser (
  input  in_1,
  output _2_pulse
);

  wire and_1_out, clock_1_out, controlled_buffer_1_out, j_k_ff_1_q, j_k_ff_1_qn, j_k_ff_2_q, j_k_ff_2_qn,
       j_k_ff_3_q, j_k_ff_3_qn, j_k_ff_4_q, j_k_ff_4_qn, j_k_ff_5_q, nand_1_out;

  Clock #(.highDuration(1), .lowDuration(1)) clock_1 (.out(clock_1_out));
  assign controlled_buffer_1_out = nand_1_out ? clock_1_out : 1'bz;  // Controlled_Buffer controlled_buffer_1
  and and_1 (and_1_out, in_1, controlled_buffer_1_out);
  J_K_Flip_Flop #(.trigger("rising")) j_k_ff_1 (
    .J(1'b1), .clk(and_1_out), .K(1'b1), .Q(j_k_ff_1_q), .Qn(j_k_ff_1_qn));  // open: preset, en, reset
  not not_1 (_2_pulse, j_k_ff_1_q);
  J_K_Flip_Flop #(.trigger("rising")) j_k_ff_2 (
    .J(1'b1), .clk(j_k_ff_1_qn), .K(1'b1), .Q(j_k_ff_2_q), .Qn(j_k_ff_2_qn));  // open: preset, en, reset
  nand nand_1 (nand_1_out, j_k_ff_1_q, j_k_ff_2_q, j_k_ff_3_q, j_k_ff_4_q, j_k_ff_5_q);
  J_K_Flip_Flop #(.trigger("rising")) j_k_ff_3 (
    .J(1'b1), .clk(j_k_ff_2_qn), .K(1'b1), .Q(j_k_ff_3_q), .Qn(j_k_ff_3_qn));  // open: preset, en, reset
  J_K_Flip_Flop #(.trigger("rising")) j_k_ff_4 (
    .J(1'b1), .clk(j_k_ff_3_qn), .K(1'b1), .Q(j_k_ff_4_q), .Qn(j_k_ff_4_qn));  // open: preset, en, reset
  J_K_Flip_Flop #(.trigger("rising")) j_k_ff_5 (
    .J(1'b1), .clk(j_k_ff_4_qn), .K(1'b1), .Q(j_k_ff_5_q));  // open: Qn, preset, en, reset
endmodule

module memory_module_4_bit (
  input  s0,
  input  s1,
  input  s2,
  input  s3,
  input  reset,
  input  cpy,
  output S0_out,
  output S1_out,
  output S2_out,
  output S3_out,
  output cpy_0,
  output cpy_1,
  output cpy_2,
  output cpy_3,
  output reset_signal
);

  wire n2_pulsers_1__2_pulse, n2_pulsers_2__2_pulse, or_1_out, or_2_out, or_3_out, or_4_out;

  _2_pulsers u_2_pulsers_1 (.pulse_input(cpy), ._2_pulse(n2_pulsers_1__2_pulse));
  _2_pulsers u_2_pulsers_2 (.pulse_input(cpy), ._2_pulse(n2_pulsers_2__2_pulse));
  _1_pulser u_1_pulser_1 (.cpy_signal(cpy), ._1_pulse(reset_signal));
  J_K_Flip_Flop #(.trigger("rising")) j_k_ff_1 (
    .J(1'b1), .clk(or_1_out), .K(1'b1), .Q(S0_out), .reset(reset));  // open: Qn, preset, en
  assign cpy_0 = n2_pulsers_2__2_pulse ? S0_out : 1'bz;  // Controlled_Buffer controlled_buffer_1
  or or_1 (or_1_out, n2_pulsers_1__2_pulse, s0);
  J_K_Flip_Flop #(.trigger("rising")) j_k_ff_2 (
    .J(1'b1), .clk(or_2_out), .K(1'b1), .Q(S1_out), .reset(reset));  // open: Qn, preset, en
  or or_2 (or_2_out, n2_pulsers_1__2_pulse, s1);
  assign cpy_1 = n2_pulsers_2__2_pulse ? S1_out : 1'bz;  // Controlled_Buffer controlled_buffer_2
  or or_3 (or_3_out, n2_pulsers_1__2_pulse, s2);
  J_K_Flip_Flop #(.trigger("rising")) j_k_ff_3 (
    .J(1'b1), .clk(or_3_out), .K(1'b1), .Q(S2_out), .reset(reset));  // open: Qn, preset, en
  assign cpy_2 = n2_pulsers_2__2_pulse ? S2_out : 1'bz;  // Controlled_Buffer controlled_buffer_3
  or or_4 (or_4_out, n2_pulsers_1__2_pulse, s3);
  J_K_Flip_Flop #(.trigger("rising")) j_k_ff_4 (
    .J(1'b1), .clk(or_4_out), .K(1'b1), .Q(S3_out), .reset(reset));  // open: Qn, preset, en
  assign cpy_3 = n2_pulsers_2__2_pulse ? S3_out : 1'bz;  // Controlled_Buffer controlled_buffer_4

  // Notes on the sheet:
  //   2 pulse
  //   1 pulse
  //   1 pulse
  //   2 pulse
  //   1 pulse
  //   1 pulse
  //   testing 4-bit RAM cpy function
  //   4 bit RAM
  //   cpy: first enable copy, then "storeage 1-8" press twice 
endmodule

module test (
  input  in_1,
  input  in_2,
  input  in_3,
  input  in_4,
  input  reset,
  input  cpy
);

  wire controlled_buffer_1_out, controlled_buffer_2_out, controlled_buffer_3_out, controlled_buffer_4_out,
       j_k_ff_1_q, j_k_ff_3_q, j_k_ff_5_q, j_k_ff_7_q, n1_pulser_1__1_pulse, n2_pulsers_1__2_pulse,
       n2_pulsers_2__2_pulse, or_1_out, or_2_out, or_3_out, or_4_out;

  _2_pulsers u_2_pulsers_1 (.pulse_input(cpy), ._2_pulse(n2_pulsers_1__2_pulse));
  _2_pulsers u_2_pulsers_2 (.pulse_input(cpy), ._2_pulse(n2_pulsers_2__2_pulse));
  _1_pulser u_1_pulser_1 (.cpy_signal(cpy), ._1_pulse(n1_pulser_1__1_pulse));
  J_K_Flip_Flop #(.trigger("rising")) j_k_ff_1 (
    .J(1'b1), .clk(or_1_out), .K(1'b1), .Q(j_k_ff_1_q), .reset(reset));  // open: Qn, preset, en
  assign controlled_buffer_1_out = n2_pulsers_2__2_pulse ? j_k_ff_1_q : 1'bz;  // Controlled_Buffer controlled_buffer_1
  J_K_Flip_Flop #(.trigger("rising")) j_k_ff_2 (
    .J(1'b1), .clk(controlled_buffer_1_out), .K(1'b1), .reset(n1_pulser_1__1_pulse));  // open: Q, Qn, preset, en
  or or_1 (or_1_out, n2_pulsers_1__2_pulse, in_1);
  J_K_Flip_Flop #(.trigger("rising")) j_k_ff_3 (
    .J(1'b1), .clk(or_2_out), .K(1'b1), .Q(j_k_ff_3_q), .reset(reset));  // open: Qn, preset, en
  J_K_Flip_Flop #(.trigger("rising")) j_k_ff_4 (
    .J(1'b1), .clk(controlled_buffer_2_out), .K(1'b1), .reset(n1_pulser_1__1_pulse));  // open: Q, Qn, preset, en
  or or_2 (or_2_out, n2_pulsers_1__2_pulse, in_2);
  assign controlled_buffer_2_out = n2_pulsers_2__2_pulse ? j_k_ff_3_q : 1'bz;  // Controlled_Buffer controlled_buffer_2
  or or_3 (or_3_out, n2_pulsers_1__2_pulse, in_3);
  J_K_Flip_Flop #(.trigger("rising")) j_k_ff_5 (
    .J(1'b1), .clk(or_3_out), .K(1'b1), .Q(j_k_ff_5_q), .reset(reset));  // open: Qn, preset, en
  assign controlled_buffer_3_out = n2_pulsers_2__2_pulse ? j_k_ff_5_q : 1'bz;  // Controlled_Buffer controlled_buffer_3
  J_K_Flip_Flop #(.trigger("rising")) j_k_ff_6 (
    .J(1'b1), .clk(controlled_buffer_3_out), .K(1'b1), .reset(n1_pulser_1__1_pulse));  // open: Q, Qn, preset, en
  or or_4 (or_4_out, n2_pulsers_1__2_pulse, in_4);
  J_K_Flip_Flop #(.trigger("rising")) j_k_ff_7 (
    .J(1'b1), .clk(or_4_out), .K(1'b1), .Q(j_k_ff_7_q), .reset(reset));  // open: Qn, preset, en
  assign controlled_buffer_4_out = n2_pulsers_2__2_pulse ? j_k_ff_7_q : 1'bz;  // Controlled_Buffer controlled_buffer_4
  J_K_Flip_Flop #(.trigger("rising")) j_k_ff_8 (
    .J(1'b1), .clk(controlled_buffer_4_out), .K(1'b1), .reset(n1_pulser_1__1_pulse));  // open: Q, Qn, preset, en

  // Notes on the sheet:
  //   cpy: first enable copy, then "storeage 1-8" press twice 
  //   testing 4-bit RAM cpy function
  //   4 bit RAM
endmodule

module test_4bit (
  input  in_1,
  input  in_2,
  input  in_3,
  input  in_4,
  input  reset,
  input  cpy,
  output out_7,
  output out_8,
  output out_9,
  output out_10,
  output out_11,
  output out_12,
  output out_13,
  output out_14
);

  wire memory_module_4_bit_1_cpy_0, memory_module_4_bit_1_cpy_1, memory_module_4_bit_1_cpy_2,
       memory_module_4_bit_1_cpy_3, memory_module_4_bit_1_reset_signal, or_1_out, or_2_out, or_3_out,
       or_4_out, or_5_out, undriven, undriven_2, undriven_3, undriven_4, undriven_5;

  or or_1 (or_1_out, reset, memory_module_4_bit_1_reset_signal);
  or or_2 (or_2_out, memory_module_4_bit_1_cpy_2, undriven_2);
  or or_3 (or_3_out, memory_module_4_bit_1_cpy_3, undriven);
  memory_module_4_bit memory_module_4_bit_1 (
    .reset(reset), .cpy(cpy), .s0(in_1), .s1(in_2), .s2(in_3), .s3(in_4), .S0_out(out_7), .S1_out(out_8),
    .S2_out(out_9), .S3_out(out_10), .cpy_0(memory_module_4_bit_1_cpy_0),
    .cpy_1(memory_module_4_bit_1_cpy_1), .cpy_2(memory_module_4_bit_1_cpy_2),
    .cpy_3(memory_module_4_bit_1_cpy_3), .reset_signal(memory_module_4_bit_1_reset_signal));
  or or_4 (or_4_out, memory_module_4_bit_1_cpy_1, undriven_3);
  memory_module_4_bit memory_module_4_bit_2 (
    .reset(or_1_out), .s0(or_3_out), .s1(or_2_out), .s2(or_4_out), .s3(undriven_4), .S0_out(out_11),
    .S1_out(out_12), .S2_out(out_13), .S3_out(out_14));  // open: cpy, cpy_0, cpy_1, cpy_2, cpy_3, reset_signal
  or or_5 (or_5_out, memory_module_4_bit_1_cpy_0, undriven_5);
endmodule
