// Logisim project input_output.circ as structural Verilog: 19 circuits, main circuit test first input/output
module test_first_input_output (
  input  write,
  input  read,
  input  in_3,
  input  in_4,
  output [6:0] out_5,
  output [3:0] out_6
);

  wire and_1_out, clock_1_out, controlled_buffer_1_out, enter_detect_1_enter, keyboard_1_avail,
       n2x56_bit_ram_16_charators_1_done;
  wire [6:0] controlled_buffer_2_out, keyboard_1_data;

  Clock #(.highDuration(1), .lowDuration(1)) clock_1 (.out(clock_1_out));
  Counter #(.width(4), .max(15), .trigger("rising")) counter_1 (
    .Q(out_6), .clk(controlled_buffer_1_out), .clr(enter_detect_1_enter));  // open: load, D, count, carry
  Keyboard #(.buflen(32), .trigger("rising")) keyboard_1 (
    .clk(controlled_buffer_1_out), .avail(keyboard_1_avail), .data(keyboard_1_data));  // open: re, clr
  assign controlled_buffer_1_out = and_1_out ? clock_1_out : 1'bz;  // Controlled_Buffer controlled_buffer_1
  and and_1 (and_1_out, n2x56_bit_ram_16_charators_1_done, keyboard_1_avail);
  assign controlled_buffer_2_out = keyboard_1_avail ? keyboard_1_data : 7'bz;  // Controlled_Buffer controlled_buffer_2
  _2x56_bit_RAM__16_charators u_2x56_bit_ram_16_charators_1 (
    .clock(clock_1_out), .write(write), .read(read), .reset(enter_detect_1_enter),
    .Sin_0_7(controlled_buffer_2_out), .done(n2x56_bit_ram_16_charators_1_done), .loc0_3(out_6),
    .out0_7(out_5));
  enter_detect enter_detect_1 (.in0_6(controlled_buffer_2_out), .enter(enter_detect_1_enter));
  TTY #(.rows(16), .cols(32), .trigger("rising")) tty_1 (
    .data(out_5), .clk(controlled_buffer_1_out), .we(in_3), .clr(in_4));
endmodule

module _2x56_bit_RAM__16_charators (
  input  [6:0] Sin_0_7,
  input  clock,
  input  write,
  input  read,
  input  reset,
  input  [3:0] loc0_3,
  output done,
  output [6:0] out0_7
);

  wire controlled_buffer_1_out, controlled_buffer_2_out, controlled_buffer_3_out, controlled_buffer_4_out,
       decoder_1_out0, decoder_1_out1, n56_bit_ram_1_done, n56_bit_ram_2_done;
  wire [2:0] controlled_buffer_5_out, controlled_buffer_6_out;
  wire [6:0] n56_bit_ram_1_out0_7, n56_bit_ram_2_out0_7;

  assign controlled_buffer_1_out = decoder_1_out0 ? write : 1'bz;  // Controlled_Buffer controlled_buffer_1
  assign controlled_buffer_2_out = decoder_1_out0 ? read : 1'bz;  // Controlled_Buffer controlled_buffer_2
  assign controlled_buffer_3_out = decoder_1_out1 ? write : 1'bz;  // Controlled_Buffer controlled_buffer_3
  assign controlled_buffer_4_out = decoder_1_out1 ? read : 1'bz;  // Controlled_Buffer controlled_buffer_4
  Decoder #(.select(1), .tristate("false")) decoder_1 (.out0(decoder_1_out0), .out1(decoder_1_out1), .sel(loc0_3[0]));
  and and_1 (done, n56_bit_ram_1_done, n56_bit_ram_2_done);
  _56_bit_RAM u_56_bit_ram_1 (
    .clock(clock), .write(controlled_buffer_1_out), .read(controlled_buffer_2_out), .Sin_0_7(Sin_0_7),
    .done(n56_bit_ram_1_done), .location(controlled_buffer_5_out), .reset(reset),
    .out0_7(n56_bit_ram_1_out0_7));
  _56_bit_RAM u_56_bit_ram_2 (
    .clock(clock), .write(controlled_buffer_3_out), .read(controlled_buffer_4_out), .Sin_0_7(Sin_0_7),
    .done(n56_bit_ram_2_done), .location(controlled_buffer_6_out), .reset(reset),
    .out0_7(n56_bit_ram_2_out0_7));
  assign controlled_buffer_5_out = decoder_1_out0 ? loc0_3[3:1] : 3'bz;  // Controlled_Buffer controlled_buffer_5
  assign controlled_buffer_6_out = decoder_1_out1 ? loc0_3[3:1] : 3'bz;  // Controlled_Buffer controlled_buffer_6
  assign out0_7 = n56_bit_ram_1_out0_7 | n56_bit_ram_2_out0_7;  // OR_Gate or_1, 7 bits wide
endmodule

module _56_bit_RAM (
  input  [2:0] location,
  input  [6:0] Sin_0_7,
  input  reset,
  input  clock,
  input  write,
  input  read,
  output [6:0] out0_7,
  output done
);

  wire and_1_out, and_2_out, and_3_out, and_4_out, and_5_out, and_6_out, and_7_out, and_8_out, and_9_out,
       and_10_out, and_11_out, and_12_out, and_13_out, and_14_out, and_15_out, and_16_out, decoder_1_out0,
       decoder_1_out1, decoder_1_out2, decoder_1_out3, decoder_1_out4, decoder_1_out5, decoder_1_out6,
       decoder_1_out7, n7_bit_ram_for_keyboard_1_done, n7_bit_ram_for_keyboard_2_done,
       n7_bit_ram_for_keyboard_3_done, n7_bit_ram_for_keyboard_4_done, n7_bit_ram_for_keyboard_5_done,
       n7_bit_ram_for_keyboard_6_done, n7_bit_ram_for_keyboard_7_done, n7_bit_ram_for_keyboard_8_done;
  wire [6:0] n7_bit_ram_for_keyboard_1_out0_6, n7_bit_ram_for_keyboard_2_out0_6,
       n7_bit_ram_for_keyboard_3_out0_6, n7_bit_ram_for_keyboard_4_out0_6, n7_bit_ram_for_keyboard_5_out0_6,
       n7_bit_ram_for_keyboard_6_out0_6, n7_bit_ram_for_keyboard_7_out0_6, n7_bit_ram_for_keyboard_8_out0_6;

  Decoder #(.select(3), .tristate("false")) decoder_1 (
    .out0(decoder_1_out0), .out1(decoder_1_out1), .out2(decoder_1_out2), .out3(decoder_1_out3),
    .out4(decoder_1_out4), .out5(decoder_1_out5), .out6(decoder_1_out6), .out7(decoder_1_out7), .sel(location));
  and and_1 (and_1_out, write, decoder_1_out0);
  and and_2 (and_2_out, decoder_1_out0, read);
  and and_3 (and_3_out, write, decoder_1_out1);
  and and_4 (and_4_out, decoder_1_out1, read);
  and and_5 (and_5_out, write, decoder_1_out2);
  and and_6 (and_6_out, decoder_1_out2, read);
  and and_7 (and_7_out, write, decoder_1_out3);
  and and_8 (and_8_out, decoder_1_out3, read);
  and and_9 (and_9_out, write, decoder_1_out4);
  and and_10 (and_10_out, decoder_1_out4, read);
  and and_11 (and_11_out, write, decoder_1_out5);
  and and_12 (and_12_out, decoder_1_out5, read);
  and and_13 (and_13_out, write, decoder_1_out6);
  and and_14 (and_14_out, decoder_1_out6, read);
  and and_15 (and_15_out, write, decoder_1_out7);
  and and_16 (and_16_out, decoder_1_out7, read);
  _7_bit_RAM_for_keyboard u_7_bit_ram_for_keyboard_1 (
    .S0_S6(Sin_0_7), .write(and_1_out), .read(and_2_out), .clock(clock), .reset(reset),
    .done(n7_bit_ram_for_keyboard_1_done), .out0_6(n7_bit_ram_for_keyboard_1_out0_6));
  _7_bit_RAM_for_keyboard u_7_bit_ram_for_keyboard_2 (
    .S0_S6(Sin_0_7), .write(and_3_out), .read(and_4_out), .clock(clock), .reset(reset),
    .done(n7_bit_ram_for_keyboard_2_done), .out0_6(n7_bit_ram_for_keyboard_2_out0_6));
  _7_bit_RAM_for_keyboard u_7_bit_ram_for_keyboard_3 (
    .S0_S6(Sin_0_7), .write(and_5_out), .read(and_6_out), .clock(clock), .reset(reset),
    .done(n7_bit_ram_for_keyboard_3_done), .out0_6(n7_bit_ram_for_keyboard_3_out0_6));
  _7_bit_RAM_for_keyboard u_7_bit_ram_for_keyboard_4 (
    .S0_S6(Sin_0_7), .write(and_7_out), .read(and_8_out), .clock(clock), .reset(reset),
    .done(n7_bit_ram_for_keyboard_4_done), .out0_6(n7_bit_ram_for_keyboard_4_out0_6));
  _7_bit_RAM_for_keyboard u_7_bit_ram_for_keyboard_5 (
    .S0_S6(Sin_0_7), .write(and_9_out), .read(and_10_out), .clock(clock), .reset(reset),
    .done(n7_bit_ram_for_keyboard_5_done), .out0_6(n7_bit_ram_for_keyboard_5_out0_6));
  _7_bit_RAM_for_keyboard u_7_bit_ram_for_keyboard_6 (
    .S0_S6(Sin_0_7), .write(and_11_out), .read(and_12_out), .clock(clock), .reset(reset),
    .done(n7_bit_ram_for_keyboard_6_done), .out0_6(n7_bit_ram_for_keyboard_6_out0_6));
  _7_bit_RAM_for_keyboard u_7_bit_ram_for_keyboard_7 (
    .S0_S6(Sin_0_7), .write(and_13_out), .read(and_14_out), .clock(clock), .reset(reset),
    .done(n7_bit_ram_for_keyboard_7_done), .out0_6(n7_bit_ram_for_keyboard_7_out0_6));
  _7_bit_RAM_for_keyboard u_7_bit_ram_for_keyboard_8 (
    .S0_S6(Sin_0_7), .write(and_15_out), .read(and_16_out), .clock(clock), .reset(reset),
    .done(n7_bit_ram_for_keyboard_8_done), .out0_6(n7_bit_ram_for_keyboard_8_out0_6));
  and and_17 (done, n7_bit_ram_for_keyboard_1_done, n7_bit_ram_for_keyboard_2_done, n7_bit_ram_for_keyboard_3_done, n7_bit_ram_for_keyboard_4_done, n7_bit_ram_for_keyboard_5_done, n7_bit_ram_for_keyboard_6_done, n7_bit_ram_for_keyboard_7_done, n7_bit_ram_for_keyboard_8_done, n7_bit_ram_for_keyboard_8_done);
  assign out0_7 = n7_bit_ram_for_keyboard_1_out0_6 | n7_bit_ram_for_keyboard_2_out0_6 | n7_bit_ram_for_keyboard_3_out0_6 | n7_bit_ram_for_keyboard_4_out0_6 | n7_bit_ram_for_keyboard_5_out0_6 | n7_bit_ram_for_keyboard_6_out0_6 | n7_bit_ram_for_keyboard_7_out0_6 | n7_bit_ram_for_keyboard_8_out0_6;  // OR_Gate or_1, 7 bits wide

  // Notes on the sheet:
  //   can store 8 charactors at a time
endmodule

module _7_bit_RAM_for_keyboard (
  input  write,
  input  clock,
  input  read,
  input  [6:0] S0_S6,
  input  reset,
  output done,
  output [6:0] out0_6
);

  wire n1_bit_ram_1_done, n1_bit_ram_2_done, n1_bit_ram_3_done, n1_bit_ram_4_done, n1_bit_ram_5_done,
       n1_bit_ram_6_done, n1_bit_ram_7_done;
  wire [6:0] controlled_buffer_1_out, n1_bit_ram_7_out;

  assign controlled_buffer_1_out = write ? S0_S6 : 7'bz;  // Controlled_Buffer controlled_buffer_1
  _1_bit_RAM u_1_bit_ram_1 (
    .set(controlled_buffer_1_out[6]), .DONE(n1_bit_ram_1_done), .clock(clock), .reset(reset),
    .out(n1_bit_ram_7_out[6]));
  _1_bit_RAM u_1_bit_ram_2 (
    .set(controlled_buffer_1_out[5]), .DONE(n1_bit_ram_2_done), .clock(clock), .reset(reset),
    .out(n1_bit_ram_7_out[5]));
  _1_bit_RAM u_1_bit_ram_3 (
    .set(controlled_buffer_1_out[4]), .DONE(n1_bit_ram_3_done), .clock(clock), .reset(reset),
    .out(n1_bit_ram_7_out[4]));
  _1_bit_RAM u_1_bit_ram_4 (
    .set(controlled_buffer_1_out[3]), .DONE(n1_bit_ram_4_done), .clock(clock), .reset(reset),
    .out(n1_bit_ram_7_out[3]));
  _1_bit_RAM u_1_bit_ram_5 (
    .set(controlled_buffer_1_out[1]), .DONE(n1_bit_ram_5_done), .clock(clock), .reset(reset),
    .out(n1_bit_ram_7_out[1]));
  _1_bit_RAM u_1_bit_ram_6 (
    .set(controlled_buffer_1_out[2]), .DONE(n1_bit_ram_6_done), .clock(clock), .reset(reset),
    .out(n1_bit_ram_7_out[2]));
  _1_bit_RAM u_1_bit_ram_7 (
    .set(controlled_buffer_1_out[0]), .DONE(n1_bit_ram_7_done), .clock(clock), .reset(reset),
    .out(n1_bit_ram_7_out[0]));
  and and_1 (done, n1_bit_ram_1_done, n1_bit_ram_2_done, n1_bit_ram_3_done, n1_bit_ram_4_done, n1_bit_ram_6_done, n1_bit_ram_5_done, n1_bit_ram_7_done);
  assign out0_6 = read ? n1_bit_ram_7_out : 7'bz;  // Controlled_Buffer controlled_buffer_2
endmodule

module _1_bit_RAM (
  input  set,
  input  clock,
  input  reset,
  output DONE,
  output out
);

  wire and_1_out, and_2_out, j_k_ff_1_q, not_1_out, set_1_set_as_0, set_1_set_as_1;

  set set_1 (.set(set), .set_as_0(set_1_set_as_0), .set_as_1(set_1_set_as_1));
  J_K_Flip_Flop #(.trigger("rising")) j_k_ff_1 (
    .J(set_1_set_as_1), .clk(clock), .K(set_1_set_as_0), .Q(j_k_ff_1_q), .reset(reset));  // open: Qn, preset, en
  not not_1 (not_1_out, j_k_ff_1_q);
  and and_1 (and_1_out, not_1_out, set_1_set_as_0);
  and and_2 (and_2_out, set_1_set_as_1, j_k_ff_1_q);
  or or_1 (DONE, and_1_out, and_2_out);
  assign out = DONE ? j_k_ff_1_q : 1'bz;  // Controlled_Buffer controlled_buffer_1

  // Notes on the sheet:
  //   states:
  //   J K 00 no change
  //   JK 01 change to 0
  //   JK 10 change to 1
  //   JK 11 
  //   invert signal (toggle)
  //   done with op signal
  //   best if dont use toggle
  //   and just use set 0 and 1
endmodule

module set (
  input  set,
  output set_as_0,
  output set_as_1
);

  Decoder #(.select(1), .tristate("false")) decoder_1 (.out0(set_as_0), .out1(set_as_1), .sel(set));
endmodule

module test_keybaord (
  input  write,
  input  read,
  output [6:0] out_3,
  output [3:0] out_4
);

  wire clock_1_out, controlled_buffer_1_out, keyboard_1_avail, n2x56_bit_ram_16_charators_1_p6;
  wire [6:0] controlled_buffer_2_out, keyboard_1_data;

  Clock #(.highDuration(1), .lowDuration(1)) clock_1 (.out(clock_1_out));
  Counter #(.width(4), .max(15), .trigger("rising")) counter_1 (
    .Q(out_4), .clk(controlled_buffer_1_out));  // open: load, D, count, carry, clr
  assign controlled_buffer_1_out = n2x56_bit_ram_16_charators_1_p6 ? clock_1_out : 1'bz;  // Controlled_Buffer controlled_buffer_1
  Keyboard #(.buflen(32), .trigger("rising")) keyboard_1 (
    .clk(controlled_buffer_1_out), .avail(keyboard_1_avail), .data(keyboard_1_data));  // open: re, clr
  assign controlled_buffer_2_out = keyboard_1_avail ? keyboard_1_data : 7'bz;  // Controlled_Buffer controlled_buffer_2
  // _2x56_bit_RAM__16_charators 2x56_bit_ram_16_charators_1: pin names not known; wires that end beside it: clock_1_out, write, read, controlled_buffer_2_out, out_4, n2x56_bit_ram_16_charators_1_p6, out_3
endmodule

module common_output (
  input  [1:0] sel,
  input  en,
  output [6:0] out_3,
  output done_signal
);

  wire and_1_out, and_2_out, and_3_out, and_4_out, char_1_done, decoder_1_out0, decoder_1_out1,
       decoder_1_out2, decoder_1_out3;
  wire [6:0] char_1_out_2;

  Decoder #(.select(2), .tristate("false")) decoder_1 (
    .out0(decoder_1_out0), .out1(decoder_1_out1), .out2(decoder_1_out2), .out3(decoder_1_out3), .sel(sel));
  and and_1 (and_1_out, decoder_1_out0, en);
  and and_2 (and_2_out, en, decoder_1_out1);
  and and_3 (and_3_out, en, decoder_1_out2);
  and and_4 (and_4_out, decoder_1_out3, en);
  char char_1 (.EN(and_1_out), .done(char_1_done), .out_2(char_1_out_2));
  assign out_3 = char_1_out_2;  // OR_Gate or_1, 7 bits wide OR_Gate
  buf or_2 (done_signal, char_1_done);  // OR_Gate
endmodule

module char (
  input  EN,
  output [6:0] out_2,
  output done
);

  assign out_2[0] = EN ? 1'b0 : 1'bz;  // Controlled_Buffer controlled_buffer_1
  assign out_2[1] = EN ? 1'b1 : 1'bz;  // Controlled_Buffer controlled_buffer_2
  assign out_2[2] = EN ? 1'b0 : 1'bz;  // Controlled_Buffer controlled_buffer_3
  assign out_2[3] = EN ? 1'b1 : 1'bz;  // Controlled_Buffer controlled_buffer_4
  assign out_2[4] = EN ? 1'b1 : 1'bz;  // Controlled_Buffer controlled_buffer_5
  assign done = EN ? 1'b1 : 1'bz;  // Controlled_Buffer controlled_buffer_6
  assign out_2[6] = EN ? 1'b0 : 1'bz;  // Controlled_Buffer controlled_buffer_7

  assign out_2[5] = done;

  // Notes on the sheet:
  //   waiting for input
endmodule

module enter_detect (
  input  [6:0] in0_6,
  output enter
);

  Comparator #(.width(7), .mode("twosComplement")) comparator_1 (
    .a(in0_6), .b(7'b0001010), .eq(enter));  // open: gt, lt

  // Notes on the sheet:
  //   0001010 is enter key
  //   compares each key and sees if it is the enter key.
  //   michael chrisco
endmodule

module backspace_detect (
  input  [6:0] in0_6,
  output enter
);

  Comparator #(.width(7), .mode("twosComplement")) comparator_1 (
    .a(in0_6), .b(7'b0001000), .eq(enter));  // open: gt, lt

  // Notes on the sheet:
  //   0001010 is enter key
  //   compares each key and sees if it is the enter key.
  //   michael chrisco
endmodule

module ADD_detected (
  input  [6:0] \input ,
  input  [1:0] loc0_2,
  input  clock,
  input  reset,
  output done,
  output ADD_dectected,
  output A,
  output D,
  output D_2
);

  wire a_detector_1_enter, d_detector_1_enter, d_detector_2_enter, decoder_1_out0, decoder_1_out1,
       decoder_1_out2, n1_bit_ram_1_done, n1_bit_ram_2_done, n1_bit_ram_3_done;
  wire [6:0] controlled_buffer_1_out, controlled_buffer_2_out, controlled_buffer_3_out;

  Decoder #(.select(2), .tristate("false")) decoder_1 (
    .out0(decoder_1_out0), .out1(decoder_1_out1), .out2(decoder_1_out2), .sel(loc0_2));  // open: out3
  assign controlled_buffer_1_out = decoder_1_out0 ? \input  : 7'bz;  // Controlled_Buffer controlled_buffer_1
  assign controlled_buffer_2_out = decoder_1_out1 ? \input  : 7'bz;  // Controlled_Buffer controlled_buffer_2
  assign controlled_buffer_3_out = decoder_1_out2 ? \input  : 7'bz;  // Controlled_Buffer controlled_buffer_3
  A_detector a_detector_1 (.in0_6(controlled_buffer_1_out), .enter(a_detector_1_enter));
  D_detector d_detector_1 (.in0_6(controlled_buffer_2_out), .enter(d_detector_1_enter));
  D_detector d_detector_2 (.in0_6(controlled_buffer_3_out), .enter(d_detector_2_enter));
  _1_bit_RAM u_1_bit_ram_1 (.set(a_detector_1_enter), .DONE(n1_bit_ram_1_done), .clock(clock), .reset(reset), .out(A));
  _1_bit_RAM u_1_bit_ram_2 (.set(d_detector_1_enter), .DONE(n1_bit_ram_2_done), .clock(clock), .reset(reset), .out(D));
  _1_bit_RAM u_1_bit_ram_3 (
    .set(d_detector_2_enter), .DONE(n1_bit_ram_3_done), .clock(clock), .reset(reset), .out(D_2));
  and and_1 (done, n1_bit_ram_1_done, n1_bit_ram_2_done, n1_bit_ram_3_done);
  and and_2 (ADD_dectected, A, D, D_2);

  // Notes on the sheet:
  //   ADD detected if 
  //   looks to see if operations are found in the  buffer
  //   make detectors out of every letter.
  //   A detect
  //   D detector
  //   D detector
endmodule

module _1_bit_pulser (
  input  cpy_signal,
  output _1_pulse
);

  wire and_1_out, clock_1_out, controlled_buffer_1_out, j_k_ff_1_q, not_1_out;

  assign controlled_buffer_1_out = not_1_out ? clock_1_out : 1'bz;  // Controlled_Buffer controlled_buffer_1
  Clock #(.highDuration(2), .lowDuration(2)) clock_1 (.out(clock_1_out));
  J_K_Flip_Flop #(.trigger("rising")) j_k_ff_1 (
    .J(1'b1), .clk(and_1_out), .K(1'b1), .Q(j_k_ff_1_q));  // open: Qn, preset, en, reset
  and and_1 (and_1_out, cpy_signal, controlled_buffer_1_out);
  not not_1 (not_1_out, j_k_ff_1_q);
  not not_2 (_1_pulse, j_k_ff_1_q);

  // Notes on the sheet:
  //   1 pulser
  //   Michael Chrisco
endmodule

module combinational_buffer_and_counter (
  input  [6:0] ASKii_value_of_char,
  input  key_clock_in,
  input  _1_when_char,
  input  write,
  input  read,
  input  reset,
  output key_clock_out,
  output [3:0] counter_out,
  output [6:0] out,
  output clockout
);

  wire and_1_out, backspace_detect_1_enter, enter_detect_1_enter, n2x56_bit_ram_16_charators_1_done;
  wire [6:0] controlled_buffer_2_out;

  Counter #(.width(4), .max(15), .trigger("rising")) counter_1 (
    .load(backspace_detect_1_enter), .Q(counter_out), .clk(clockout), .clr(enter_detect_1_enter));  // open: D, count, carry
  assign clockout = and_1_out ? key_clock_in : 1'bz;  // Controlled_Buffer controlled_buffer_1
  and and_1 (and_1_out, n2x56_bit_ram_16_charators_1_done, _1_when_char);
  assign controlled_buffer_2_out = _1_when_char ? ASKii_value_of_char : 7'bz;  // Controlled_Buffer controlled_buffer_2
  _2x56_bit_RAM__16_charators u_2x56_bit_ram_16_charators_1 (
    .clock(key_clock_in), .write(write), .read(read), .reset(reset), .Sin_0_7(controlled_buffer_2_out),
    .done(n2x56_bit_ram_16_charators_1_done), .loc0_3(counter_out), .out0_7(out));
  enter_detect enter_detect_1 (.in0_6(controlled_buffer_2_out), .enter(enter_detect_1_enter));
  backspace_detect backspace_detect_1 (.in0_6(controlled_buffer_2_out), .enter(backspace_detect_1_enter));

  assign key_clock_out = clockout;

  // Notes on the sheet:
  //   test of buffer and counter
  //   computations and connections to inptu/output
  //   detects if enter key pressed
  //   detects if backspace is pressed, if so makes clock go backwards 1
endmodule

module test_of_counter_and_buffer_current (
  input  read,
  input  write,
  input  EN_out,
  output [3:0] _1_when_char
);

  wire clock_1_out, combinational_buffer_and_counter_1_clockout,
       combinational_buffer_and_counter_1_key_clock_out, keyboard_1_avail;
  wire [6:0] combinational_buffer_and_counter_1_out, keyboard_1_data;

  Clock #(.highDuration(1), .lowDuration(1)) clock_1 (.out(clock_1_out));
  combinational_buffer_and_counter combinational_buffer_and_counter_1 (
    .key_clock_in(clock_1_out), ._1_when_char(keyboard_1_avail), .ASKii_value_of_char(keyboard_1_data),
    .write(read), .read(write), .key_clock_out(combinational_buffer_and_counter_1_key_clock_out),
    .counter_out(_1_when_char), .out(combinational_buffer_and_counter_1_out),
    .clockout(combinational_buffer_and_counter_1_clockout));  // open: reset
  Keyboard #(.buflen(32), .trigger("rising")) keyboard_1 (
    .clk(combinational_buffer_and_counter_1_key_clock_out), .avail(keyboard_1_avail), .data(keyboard_1_data));  // open: re, clr
  TTY #(.rows(16), .cols(32), .trigger("rising")) tty_1 (
    .data(combinational_buffer_and_counter_1_out), .clk(combinational_buffer_and_counter_1_clockout),
    .we(EN_out));  // open: clr

  // Notes on the sheet:
  //   test of buffer and counter
endmodule

module A_detector (
  input  [6:0] in0_6,
  output enter
);

  Comparator #(.width(7), .mode("twosComplement")) comparator_1 (
    .a(in0_6), .b(7'b1000001), .eq(enter));  // open: gt, lt

  // Notes on the sheet:
  //   0001010 is enter key
  //   compares each key and sees if it is the enter key.
  //   michael chrisco
endmodule

module D_detector (
  input  [6:0] in0_6,
  output enter
);

  Comparator #(.width(7), .mode("twosComplement")) comparator_1 (
    .a(in0_6), .b(7'b1000100), .eq(enter));  // open: gt, lt

  // Notes on the sheet:
  //   0001010 is enter key
  //   compares each key and sees if it is the enter key.
  //   michael chrisco
endmodule

module pattern_matching (
  input  reset,
  output dectection_made,
  output A_char,
  output D,
  output D_2
);

  wire add_detected_1_done, clock_1_out, controlled_buffer_1_out, keyboard_1_avail;
  wire [1:0] counter_1_q;
  wire [6:0] controlled_buffer_2_out, keyboard_1_data;

  Clock #(.highDuration(1), .lowDuration(1)) clock_1 (.out(clock_1_out));
  Counter #(.width(2), .max(2), .trigger("falling")) counter_1 (
    .Q(counter_1_q), .clk(keyboard_1_avail));  // open: load, D, count, carry, clr
  assign controlled_buffer_1_out = add_detected_1_done ? clock_1_out : 1'bz;  // Controlled_Buffer controlled_buffer_1
  Keyboard #(.buflen(32), .trigger("rising")) keyboard_1 (
    .clk(controlled_buffer_1_out), .avail(keyboard_1_avail), .data(keyboard_1_data));  // open: re, clr
  ADD_detected add_detected_1 (
    .clock(clock_1_out), .done(add_detected_1_done), .ADD_dectected(dectection_made),
    .\input (controlled_buffer_2_out), .loc0_2(counter_1_q), .reset(reset), .A(A_char), .D(D), .D_2(D_2));
  assign controlled_buffer_2_out = keyboard_1_avail ? keyboard_1_data : 7'bz;  // Controlled_Buffer controlled_buffer_2

  // Notes on the sheet:
  //   use keybaord to find if commands are executed. If located, do operation in another circuit
  //   ADD
endmodule

module buffer_and_temp_data (
);

  wire [6:0] undriven;

  _2x56_bit_RAM__16_charators u_2x56_bit_ram_16_charators_1 (.Sin_0_7(undriven));  // open: clock, write, read, reset, done, loc0_3, out0_7
  _2x56_bit_RAM__16_charators u_2x56_bit_ram_16_charators_2 (.Sin_0_7(undriven));  // open: clock, write, read, reset, done, loc0_3, out0_7
endmodule
