// Logisim project 1 bit (new and improved).circ as structural Verilog: 3 circuits, main circuit 1 bit RAM
module _1_bit_RAM (
  input  set,
  input  clock,
  output DONE,
  output out
);

  wire and_1_out, and_2_out, j_k_ff_1_q, not_1_out, set_1_set_as_0, set_1_set_as_1;

  set set_1 (.set(set), .set_as_0(set_1_set_as_0), .set_as_1(set_1_set_as_1));
  J_K_Flip_Flop #(.trigger("rising")) j_k_ff_1 (
    .J(set_1_set_as_1), .clk(clock), .K(set_1_set_as_0), .Q(j_k_ff_1_q));  // open: Qn, preset, en, reset
  not not_1 (not_1_out, j_k_ff_1_q);
  and and_1 (and_1_out, not_1_out, set_1_set_as_0);
  and and_2 (and_2_out, set_1_set_as_1, j_k_ff_1_q);
  or or_1 (DONE, and_1_out, and_2_out);
  assign out = DONE ? j_k_ff_1_q : 1'bz;  // Controlled_Buffer controlled_buffer_1

  // Notes on the sheet:
  //   states:
  //   J K 00 no change
  //   JK 01 change to 0
  //   JK 10 change to 1
  //   JK 11 
  //   invert signal (toggle)
  //   done with op signal
  //   best if dont use toggle
  //   and just use set 0 and 1
endmodule

module set (
  input  set,
  output set_as_0,
  output set_as_1
);

  Decoder #(.select(1), .tristate("false")) decoder_1 (.out0(set_as_0), .out1(set_as_1), .sel(set));
endmodule

module _1_bit_with_toggle (
  input  set,
  input  clock,
  input  EN_toggle,
  output DONE,
  output out
);

  wire and_1_out, and_2_out, and_3_out, controlled_buffer_1_out, controlled_buffer_2_out, j_k_ff_1_q,
       not_1_out, not_2_out, or_1_out, or_2_out, set_1_set_as_0, set_1_set_as_1;

  set set_1 (.set(set), .set_as_0(set_1_set_as_0), .set_as_1(set_1_set_as_1));
  assign controlled_buffer_1_out = not_1_out ? set_1_set_as_0 : 1'bz;  // Controlled_Buffer controlled_buffer_1
  not not_1 (not_1_out, EN_toggle);
  assign controlled_buffer_2_out = not_1_out ? set_1_set_as_1 : 1'bz;  // Controlled_Buffer controlled_buffer_2
  J_K_Flip_Flop #(.trigger("rising")) j_k_ff_1 (
    .J(or_2_out), .clk(clock), .K(or_1_out), .Q(j_k_ff_1_q));  // open: Qn, preset, en, reset
  or or_1 (or_1_out, controlled_buffer_1_out, EN_toggle);
  or or_2 (or_2_out, controlled_buffer_2_out, EN_toggle);
  not not_2 (not_2_out, j_k_ff_1_q);
  and and_1 (and_1_out, not_2_out, set_1_set_as_0);
  and and_2 (and_2_out, set_1_set_as_1, j_k_ff_1_q);
  and and_3 (and_3_out, or_1_out, or_2_out);
  or or_3 (DONE, and_1_out, and_2_out, and_3_out);
  assign out = DONE ? j_k_ff_1_q : 1'bz;  // Controlled_Buffer controlled_buffer_3

  // Notes on the sheet:
  //   1 bit with toggle 
  //   done with op signal
endmodule
