// Logisim project 2 bit RAM.circ as structural Verilog: 3 circuits, main circuit main
module main (
  input  s0,
  input  s1,
  input  reset,
  input  cpy,
  output S0_out,
  output S1_out,
  output cpy_0,
  output cpy_1,
  output reset_signal
);

  wire n2_pulsers_1__2_pulse, n2_pulsers_2__2_pulse, or_1_out, or_2_out;

  _2_pulsers u_2_pulsers_1 (.in_1(cpy), ._2_pulse(n2_pulsers_1__2_pulse));
  _2_pulsers u_2_pulsers_2 (.in_1(cpy), ._2_pulse(n2_pulsers_2__2_pulse));
  _1_pulser u_1_pulser_1 (.cpy_signal(cpy), ._1_pulse(reset_signal));
  J_K_Flip_Flop #(.trigger("rising")) j_k_ff_1 (
    .J(1'b1), .clk(or_1_out), .K(1'b1), .Q(S0_out), .reset(reset));  // open: Qn, preset, en
  assign cpy_0 = n2_pulsers_2__2_pulse ? S0_out : 1'bz;  // Controlled_Buffer controlled_buffer_1
  or or_1 (or_1_out, n2_pulsers_1__2_pulse, s0);
  J_K_Flip_Flop #(.trigger("rising")) j_k_ff_2 (
    .J(1'b1), .clk(or_2_out), .K(1'b1), .Q(S1_out), .reset(reset));  // open: Qn, preset, en
  or or_2 (or_2_out, n2_pulsers_1__2_pulse, s1);
  assign cpy_1 = n2_pulsers_2__2_pulse ? S1_out : 1'bz;  // Controlled_Buffer controlled_buffer_2

  // Notes on the sheet:
  //   2 pulse
  //   1 pulse
  //   1 pulse
  //   2 pulse
  //   1 pulse
  //   1 pulse
  //   2 bit RAM
  //   Michael Chrisco
  //   1. has reset for initialization.
  //   3. individual cells have storage capability
  //   2. copy is cpy and copies current data via pulses to next 4 bit RAM
  //   cpy: first enable copy, then "storeage 1-8" press twice 
  //   2 bit RAM
endmodule

module _2_pulsers (
  input  in_1,
  output _2_pulse
);

  wire and_1_out, clock_1_out, controlled_buffer_1_out, j_k_ff_1_q, j_k_ff_1_qn, j_k_ff_2_q, nand_1_out;

  Clock #(.highDuration(1), .lowDuration(1)) clock_1 (.out(clock_1_out));
  assign controlled_buffer_1_out = nand_1_out ? clock_1_out : 1'bz;  // Controlled_Buffer controlled_buffer_1
  J_K_Flip_Flop #(.trigger("rising")) j_k_ff_1 (
    .J(1'b1), .clk(and_1_out), .K(1'b1), .Q(j_k_ff_1_q), .Qn(j_k_ff_1_qn));  // open: preset, en, reset
  and and_1 (and_1_out, in_1, controlled_buffer_1_out);
  nand nand_1 (nand_1_out, j_k_ff_2_q, j_k_ff_1_q);
  not not_1 (_2_pulse, j_k_ff_1_q);
  J_K_Flip_Flop #(.trigger("rising")) j_k_ff_2 (
    .J(1'b1), .clk(j_k_ff_1_qn), .K(1'b1), .Q(j_k_ff_2_q));  // open: Qn, preset, en, reset
endmodule

module _1_pulser (
  input  cpy_signal,
  output _1_pulse
);

  wire and_1_out, clock_1_out, controlled_buffer_1_out, j_k_ff_1_q, not_1_out;

  assign controlled_buffer_1_out = not_1_out ? clock_1_out : 1'bz;  // Controlled_Buffer controlled_buffer_1
  Clock #(.highDuration(1), .lowDuration(1)) clock_1 (.out(clock_1_out));
  J_K_Flip_Flop #(.trigger("rising")) j_k_ff_1 (
    .J(1'b1), .clk(and_1_out), .K(1'b1), .Q(j_k_ff_1_q));  // open: Qn, preset, en, reset
  and and_1 (and_1_out, cpy_signal, controlled_buffer_1_out);
  not not_1 (not_1_out, j_k_ff_1_q);
  not not_2 (_1_pulse, j_k_ff_1_q);

  // Notes on the sheet:
  //   1 pulser
  //   Michael Chrisco
endmodule
