// Logisim project 4 bit RAM_NEW.circ as structural Verilog: 1 circuit, main circuit main
module main (
  input  S0in,
  input  S1in,
  input  S2in,
  input  S3in,
  input  write,
  input  clock,
  input  read,
  output done,
  output S0out,
  output S1out,
  output S2out,
  output S2out_2
);

  wire buffer_1_out, buffer_2_out, controlled_buffer_1_out, controlled_buffer_2_out, controlled_buffer_3_out,
       controlled_buffer_4_out, n1_bit_ram_1_done, n1_bit_ram_1_out, n1_bit_ram_2_done, n1_bit_ram_2_out,
       n1_bit_ram_3_done, n1_bit_ram_3_out, n1_bit_ram_4_done, n1_bit_ram_4_out;

  _1_bit_RAM u_1_bit_ram_1 (
    .set(controlled_buffer_1_out), .DONE(n1_bit_ram_1_done), .clock(clock), .out(n1_bit_ram_1_out));
  assign controlled_buffer_1_out = write ? S0in : 1'bz;  // Controlled_Buffer controlled_buffer_1
  assign controlled_buffer_2_out = write ? S1in : 1'bz;  // Controlled_Buffer controlled_buffer_2
  assign controlled_buffer_3_out = write ? S2in : 1'bz;  // Controlled_Buffer controlled_buffer_3
  assign controlled_buffer_4_out = write ? S3in : 1'bz;  // Controlled_Buffer controlled_buffer_4
  _1_bit_RAM u_1_bit_ram_2 (
    .set(controlled_buffer_2_out), .DONE(n1_bit_ram_2_done), .clock(clock), .out(n1_bit_ram_2_out));
  buf buffer_1 (buffer_1_out, read);
  _1_bit_RAM u_1_bit_ram_3 (
    .set(controlled_buffer_3_out), .DONE(n1_bit_ram_3_done), .clock(clock), .out(n1_bit_ram_3_out));
  buf buffer_2 (buffer_2_out, buffer_1_out);
  _1_bit_RAM u_1_bit_ram_4 (
    .set(controlled_buffer_4_out), .DONE(n1_bit_ram_4_done), .clock(clock), .out(n1_bit_ram_4_out));
  and and_1 (done, n1_bit_ram_1_done, n1_bit_ram_2_done, n1_bit_ram_3_done, n1_bit_ram_4_done);
  assign S0out = buffer_2_out ? n1_bit_ram_1_out : 1'bz;  // Controlled_Buffer controlled_buffer_5
  assign S1out = buffer_2_out ? n1_bit_ram_2_out : 1'bz;  // Controlled_Buffer controlled_buffer_6
  assign S2out = buffer_2_out ? n1_bit_ram_3_out : 1'bz;  // Controlled_Buffer controlled_buffer_7
  assign S2out_2 = buffer_2_out ? n1_bit_ram_4_out : 1'bz;  // Controlled_Buffer controlled_buffer_8
endmodule
