// Logisim project RAM MATRIX 16-4 bit.circ as structural Verilog: 4 circuits, main circuit 8-4bit RAM MATRIX
module _8_4bit_RAM_MATRIX (
  input  P0,
  input  P1,
  input  P2,
  input  R_WR,
  input  EN,
  input  S0,
  input  S1,
  input  S2,
  input  S3,
  input  in_10,
  output done,
  output out_12,
  output out_13,
  output out_14,
  output S3_2
);

  wire and_2_out, main_1_done, main_1_s0out, main_1_s1out, main_1_s2out, main_1_s2out_2, main_2_done,
       main_2_s0out, main_2_s1out, main_2_s2out, main_2_s2out_2, main_3_done, main_3_s0out, main_3_s1out,
       main_3_s2out, main_3_s2out_2, main_4_done, main_4_s0out, main_4_s1out, main_4_s2out, main_4_s2out_2,
       main_5_done, main_5_s0out, main_5_s1out, main_5_s2out, main_5_s2out_2, main_6_done, main_6_s0out,
       main_6_s1out, main_6_s2out, main_6_s2out_2, main_7_done, main_7_s0out, main_7_s1out, main_7_s2out,
       main_7_s2out_2, main_8_done, main_8_s0out, main_8_s1out, main_8_s2out, main_8_s2out_2,
       mapping_system_1_r0, mapping_system_1_r1, mapping_system_1_r2, mapping_system_1_r3,
       mapping_system_1_r4, mapping_system_1_r5, mapping_system_1_r6, mapping_system_1_r7,
       mapping_system_1_w0, mapping_system_1_w1, mapping_system_1_w2, mapping_system_1_w3,
       mapping_system_1_w4, mapping_system_1_w5, mapping_system_1_w6, mapping_system_1_w7;

  mapping_system mapping_system_1 (
    .P0(P0), .P1(P1), .P2(P2), .R_WR(R_WR), .EN(EN), .W0(mapping_system_1_w0), .R0(mapping_system_1_r0),
    .W1(mapping_system_1_w1), .R1(mapping_system_1_r1), .W2(mapping_system_1_w2), .R2(mapping_system_1_r2),
    .W3(mapping_system_1_w3), .R3(mapping_system_1_r3), .W4(mapping_system_1_w4), .R4(mapping_system_1_r4),
    .W5(mapping_system_1_w5), .R5(mapping_system_1_r5), .W6(mapping_system_1_w6), .R6(mapping_system_1_r6),
    .W7(mapping_system_1_w7), .R7(mapping_system_1_r7));
  _4_bit_RAM_NEW_main main_1 (
    .S0in(S0), .S1in(S1), .S2in(S2), .S3in(S3), .write(mapping_system_1_w6), .clock(in_10),
    .read(mapping_system_1_r6), .done(main_1_done), .S0out(main_1_s0out), .S1out(main_1_s1out),
    .S2out(main_1_s2out), .S2out_2(main_1_s2out_2));
  _4_bit_RAM_NEW_main main_2 (
    .S0in(S0), .S1in(S1), .S2in(S2), .S3in(S3), .write(mapping_system_1_w7), .clock(in_10),
    .read(mapping_system_1_r7), .done(main_2_done), .S0out(main_2_s0out), .S1out(main_2_s1out),
    .S2out(main_2_s2out), .S2out_2(main_2_s2out_2));
  _4_bit_RAM_NEW_main main_3 (
    .S0in(S0), .S1in(S1), .S2in(S2), .S3in(S3), .write(mapping_system_1_w0), .clock(in_10),
    .read(mapping_system_1_r0), .done(main_3_done), .S0out(main_3_s0out), .S1out(main_3_s1out),
    .S2out(main_3_s2out), .S2out_2(main_3_s2out_2));
  _4_bit_RAM_NEW_main main_4 (
    .S0in(S0), .S1in(S1), .S2in(S2), .S3in(S3), .write(mapping_system_1_w1), .clock(in_10),
    .read(mapping_system_1_r1), .done(main_4_done), .S0out(main_4_s0out), .S1out(main_4_s1out),
    .S2out(main_4_s2out), .S2out_2(main_4_s2out_2));
  _4_bit_RAM_NEW_main main_5 (
    .S0in(S0), .S1in(S1), .S2in(S2), .S3in(S3), .write(mapping_system_1_w2), .clock(in_10),
    .read(mapping_system_1_r2), .done(main_5_done), .S0out(main_5_s0out), .S1out(main_5_s1out),
    .S2out(main_5_s2out), .S2out_2(main_5_s2out_2));
  _4_bit_RAM_NEW_main main_6 (
    .S0in(S0), .S1in(S1), .S2in(S2), .S3in(S3), .write(mapping_system_1_w3), .clock(in_10),
    .read(mapping_system_1_r3), .done(main_6_done), .S0out(main_6_s0out), .S1out(main_6_s1out),
    .S2out(main_6_s2out), .S2out_2(main_6_s2out_2));
  _4_bit_RAM_NEW_main main_7 (
    .S0in(S0), .S1in(S1), .S2in(S2), .S3in(S3), .write(mapping_system_1_w4), .clock(in_10),
    .read(mapping_system_1_r4), .done(main_7_done), .S0out(main_7_s0out), .S1out(main_7_s1out),
    .S2out(main_7_s2out), .S2out_2(main_7_s2out_2));
  _4_bit_RAM_NEW_main main_8 (
    .S0in(S0), .S1in(S1), .S2in(S2), .S3in(S3), .write(mapping_system_1_w5), .clock(in_10),
    .read(mapping_system_1_r5), .done(main_8_done), .S0out(main_8_s0out), .S1out(main_8_s1out),
    .S2out(main_8_s2out), .S2out_2(main_8_s2out_2));
  and and_1 (done, main_2_done, and_2_out);
  and and_2 (and_2_out, main_1_done, main_3_done, main_4_done, main_5_done, main_6_done, main_7_done, main_8_done);
  or or_1 (out_12, main_8_s0out, main_7_s0out, main_6_s0out, main_5_s0out, main_4_s0out, main_3_s0out, main_1_s0out, main_2_s0out);
  or or_2 (out_13, main_8_s1out, main_7_s1out, main_6_s1out, main_5_s1out, main_4_s1out, main_3_s1out, main_1_s1out, main_2_s1out);
  or or_3 (out_14, main_8_s2out, main_7_s2out, main_6_s2out, main_5_s2out, main_4_s2out, main_3_s2out, main_1_s2out, main_2_s2out);
  or or_4 (S3_2, main_8_s2out_2, main_7_s2out_2, main_6_s2out_2, main_5_s2out_2, main_4_s2out_2, main_3_s2out_2, main_1_s2out_2, main_2_s2out_2);

  // Notes on the sheet:
  //   S0
  //   S1
  //   S2
endmodule

module mapping_system (
  input  P0,
  input  P1,
  input  P2,
  input  EN,
  input  R_WR,
  output W0,
  output R0,
  output W1,
  output R1,
  output W2,
  output R2,
  output W3,
  output R3,
  output W4,
  output R4,
  output W5,
  output R5,
  output W6,
  output R6,
  output W7,
  output R7
);

  wire and_1_out, and_2_out, and_3_out, and_4_out, and_5_out, and_6_out, and_7_out, and_8_out, and_9_out,
       and_10_out, and_11_out, and_12_out, and_13_out, and_14_out, and_15_out, and_16_out, and_17_out,
       and_18_out, and_19_out, and_20_out, and_21_out, and_22_out, and_23_out, and_24_out, not_1_out,
       not_2_out, not_3_out;

  not not_1 (not_1_out, P0);
  not not_2 (not_2_out, P1);
  not not_3 (not_3_out, P2);
  and and_1 (and_1_out, not_1_out, not_2_out, not_3_out);
  and and_2 (and_2_out, not_1_out, not_2_out, P2);
  and and_3 (and_3_out, not_1_out, P1, P2);
  and and_4 (and_4_out, not_1_out, not_3_out, P1);
  and and_5 (and_5_out, P0, not_3_out, P1);
  and and_6 (and_6_out, P0, P1, P2);
  and and_7 (and_7_out, P0, not_2_out, P2);
  and and_8 (and_8_out, P0, not_2_out, not_3_out);
  and and_9 (and_9_out, EN, and_1_out);
  and and_10 (and_10_out, EN, and_2_out);
  and and_11 (and_11_out, EN, and_3_out);
  and and_12 (and_12_out, EN, and_4_out);
  and and_13 (and_13_out, EN, and_5_out);
  and and_14 (and_14_out, EN, and_6_out);
  and and_15 (and_15_out, EN, and_7_out);
  and and_16 (and_16_out, EN, and_8_out);
  assign W0 = and_9_out ? and_17_out : 1'bz;  // Controlled_Buffer controlled_buffer_1
  and and_17 (and_17_out, and_1_out, R_WR);
  and and_18 (and_18_out, and_2_out, R_WR);
  assign W1 = and_10_out ? and_18_out : 1'bz;  // Controlled_Buffer controlled_buffer_2
  assign W2 = and_11_out ? and_19_out : 1'bz;  // Controlled_Buffer controlled_buffer_3
  and and_19 (and_19_out, and_3_out, R_WR);
  and and_20 (and_20_out, and_4_out, R_WR);
  assign W3 = and_12_out ? and_20_out : 1'bz;  // Controlled_Buffer controlled_buffer_4
  and and_21 (and_21_out, and_5_out, R_WR);
  assign W4 = and_13_out ? and_21_out : 1'bz;  // Controlled_Buffer controlled_buffer_5
  assign W5 = and_14_out ? and_22_out : 1'bz;  // Controlled_Buffer controlled_buffer_6
  and and_22 (and_22_out, and_6_out, R_WR);
  and and_23 (and_23_out, and_7_out, R_WR);
  assign W6 = and_15_out ? and_23_out : 1'bz;  // Controlled_Buffer controlled_buffer_7
  and and_24 (and_24_out, and_8_out, R_WR);
  assign W7 = and_16_out ? and_24_out : 1'bz;  // Controlled_Buffer controlled_buffer_8
  not not_4 (R0, W0);
  not not_5 (R1, W1);
  not not_6 (R2, W2);
  not not_7 (R3, W3);
  not not_8 (R4, W4);
  not not_9 (R5, W5);
  not not_10 (R6, W6);
  not not_11 (R7, W7);

  // Notes on the sheet:
  //   last 2 not used (can be used some other way)
endmodule

module test (
  input  in_1,
  input  in_2,
  input  in_3,
  input  in_4,
  input  in_5,
  input  in_6,
  input  in_7,
  input  in_8,
  input  in_9,
  output out_10,
  output out_11,
  output out_12,
  output out_13
);

  wire controlled_buffer_1_out, main_1_s0, main_1_s1, main_1_s2, n8_4bit_ram_matrix_1_done;

  assign controlled_buffer_1_out = n8_4bit_ram_matrix_1_done ? in_2 : 1'bz;  // Controlled_Buffer controlled_buffer_1
  up_down_binary_counter_main main_1 (
    ._0_up_1_down(in_1), .clock(controlled_buffer_1_out), .in_3(in_3), .S0(main_1_s0), .S1(main_1_s1),
    .S2(main_1_s2));  // open: out_4, out_5
  _8_4bit_RAM_MATRIX u_8_4bit_ram_matrix_1 (
    .P0(main_1_s0), .P1(main_1_s1), .P2(main_1_s2), .R_WR(in_4), .EN(in_5), .S0(in_6), .S1(in_7), .S2(in_8),
    .S3(in_9), .done(n8_4bit_ram_matrix_1_done), .out_12(out_10), .out_13(out_11), .out_14(out_12),
    .S3_2(out_13));  // open: in_10
endmodule

module _16_4_bit_RAM_MATRIX (
  input  P0,
  input  P1,
  input  P2,
  input  P3,
  input  in_5,
  input  S0,
  input  S1,
  input  S2,
  input  S3,
  input  EN,
  output out_11,
  output out_12,
  output out_13,
  output out_14,
  output done
);

  wire clock_1_out, controlled_buffer_1_out, controlled_buffer_2_out, controlled_buffer_3_out,
       controlled_buffer_4_out, controlled_buffer_5_out, controlled_buffer_6_out, controlled_buffer_7_out,
       controlled_buffer_8_out, controlled_buffer_9_out, controlled_buffer_10_out, n8_4bit_ram_matrix_1_done,
       n8_4bit_ram_matrix_1_out_12, n8_4bit_ram_matrix_1_out_13, n8_4bit_ram_matrix_1_out_14,
       n8_4bit_ram_matrix_1_s3_2, n8_4bit_ram_matrix_2_done, n8_4bit_ram_matrix_2_out_12,
       n8_4bit_ram_matrix_2_out_13, n8_4bit_ram_matrix_2_out_14, n8_4bit_ram_matrix_2_s3_2, not_1_out,
       or_1_out, or_2_out, or_3_out, or_4_out;

  assign controlled_buffer_1_out = EN ? P3 : 1'bz;  // Controlled_Buffer controlled_buffer_1
  assign controlled_buffer_2_out = EN ? in_5 : 1'bz;  // Controlled_Buffer controlled_buffer_2
  assign controlled_buffer_3_out = EN ? S0 : 1'bz;  // Controlled_Buffer controlled_buffer_3
  assign controlled_buffer_4_out = EN ? S1 : 1'bz;  // Controlled_Buffer controlled_buffer_4
  assign controlled_buffer_5_out = EN ? S2 : 1'bz;  // Controlled_Buffer controlled_buffer_5
  assign controlled_buffer_6_out = EN ? S3 : 1'bz;  // Controlled_Buffer controlled_buffer_6
  assign controlled_buffer_7_out = EN ? P0 : 1'bz;  // Controlled_Buffer controlled_buffer_7
  assign controlled_buffer_8_out = EN ? P1 : 1'bz;  // Controlled_Buffer controlled_buffer_8
  assign controlled_buffer_9_out = EN ? P2 : 1'bz;  // Controlled_Buffer controlled_buffer_9
  not not_1 (not_1_out, controlled_buffer_1_out);
  and and_1 (done, n8_4bit_ram_matrix_2_done, n8_4bit_ram_matrix_1_done);
  _8_4bit_RAM_MATRIX u_8_4bit_ram_matrix_1 (
    .P0(controlled_buffer_7_out), .P1(controlled_buffer_8_out), .P2(controlled_buffer_9_out),
    .R_WR(controlled_buffer_2_out), .EN(not_1_out), .S0(controlled_buffer_3_out),
    .S1(controlled_buffer_4_out), .S2(controlled_buffer_5_out), .S3(controlled_buffer_6_out),
    .done(n8_4bit_ram_matrix_1_done), .in_10(controlled_buffer_10_out), .out_12(n8_4bit_ram_matrix_1_out_12),
    .out_13(n8_4bit_ram_matrix_1_out_13), .out_14(n8_4bit_ram_matrix_1_out_14),
    .S3_2(n8_4bit_ram_matrix_1_s3_2));
  _8_4bit_RAM_MATRIX u_8_4bit_ram_matrix_2 (
    .P0(controlled_buffer_7_out), .P1(controlled_buffer_8_out), .P2(controlled_buffer_9_out),
    .R_WR(controlled_buffer_2_out), .EN(controlled_buffer_1_out), .S0(controlled_buffer_3_out),
    .S1(controlled_buffer_4_out), .S2(controlled_buffer_5_out), .S3(controlled_buffer_6_out),
    .done(n8_4bit_ram_matrix_2_done), .in_10(controlled_buffer_10_out), .out_12(n8_4bit_ram_matrix_2_out_12),
    .out_13(n8_4bit_ram_matrix_2_out_13), .out_14(n8_4bit_ram_matrix_2_out_14),
    .S3_2(n8_4bit_ram_matrix_2_s3_2));
  assign controlled_buffer_10_out = done ? clock_1_out : 1'bz;  // Controlled_Buffer controlled_buffer_10
  Clock #(.highDuration(1), .lowDuration(1)) clock_1 (.out(clock_1_out));
  assign out_11 = EN ? or_1_out : 1'bz;  // Controlled_Buffer controlled_buffer_11
  assign out_12 = EN ? or_2_out : 1'bz;  // Controlled_Buffer controlled_buffer_12
  or or_1 (or_1_out, n8_4bit_ram_matrix_1_out_12, n8_4bit_ram_matrix_2_out_12);
  or or_2 (or_2_out, n8_4bit_ram_matrix_1_out_13, n8_4bit_ram_matrix_2_out_13);
  assign out_13 = EN ? or_3_out : 1'bz;  // Controlled_Buffer controlled_buffer_13
  or or_3 (or_3_out, n8_4bit_ram_matrix_1_out_14, n8_4bit_ram_matrix_2_out_14);
  assign out_14 = EN ? or_4_out : 1'bz;  // Controlled_Buffer controlled_buffer_14
  or or_4 (or_4_out, n8_4bit_ram_matrix_1_s3_2, n8_4bit_ram_matrix_2_s3_2);

  // Notes on the sheet:
  //   combinational 2 8-4 bit RAM
  //   aka 16-4 bit RAM
endmodule
