// Logisim project 2-1 MUX combinational 4-1 MUX.circ as structural Verilog: 1 circuit, main circuit main
module main (
  input  IN_2,
  input  IN_3,
  input  E,
  input  S0,
  input  S1,
  output out_6
);

  wire IN_0_out, IN_1_out, main_1_out, main_2_out;

  Clock #(.highDuration(1), .lowDuration(1)) IN_0 (.out(IN_0_out));
  Clock #(.highDuration(2), .lowDuration(2)) IN_1 (.out(IN_1_out));
  _2_1_MUX_main main_1 (.In_0(IN_0_out), .IN_1(IN_1_out), .S0(S0), .E(E), .Out(main_1_out));
  _2_1_MUX_main main_2 (.In_0(IN_2), .IN_1(IN_3), .S0(S0), .E(E), .Out(main_2_out));
  _2_1_MUX_main main_3 (.In_0(main_1_out), .IN_1(main_2_out), .S0(S1), .E(E), .Out(out_6));

  // Notes on the sheet:
  //   2-1 MUX A
  //   2-1 MUX B
  //   2-1 MUX C
endmodule
