// Logisim project 4-1 MUX test(works).circ as structural Verilog: 1 circuit, main circuit main
module main (
  input  in_1,
  input  in_2,
  input  in_3,
  output out_4
);

  wire clock_1_out, clock_2_out, clock_3_out, clock_4_out;

  Clock #(.highDuration(1), .lowDuration(1)) clock_1 (.out(clock_1_out));
  Clock #(.highDuration(2), .lowDuration(2)) clock_2 (.out(clock_2_out));
  Clock #(.highDuration(3), .lowDuration(3)) clock_3 (.out(clock_3_out));
  Clock #(.highDuration(4), .lowDuration(4)) clock_4 (.out(clock_4_out));
  _4_1_MUX__1enable__main main_1 (
    .In_0(clock_1_out), .In_1(clock_2_out), .In_2(clock_3_out), .In_3(clock_4_out), .S1(in_1), .S2(in_2),
    .E(in_3), .Out_0(out_4));
endmodule
